// Logisim project P0.circ as structural Verilog: 18 circuits, main circuit main
module CRC__divider (
  input  [3:0] Dividend,
  input  [3:0] Divisor,
  output out_3,
  output [2:0] out_4
);

  wire [3:0] and_1_out;
  wire [3:3] xor_1_out;

  assign and_1_out = {4{Dividend[3]}} & Divisor;  // AND_Gate and_1, 4 bits wide
  assign {xor_1_out[3], out_4} = and_1_out ^ Dividend;  // XOR_Gate xor_1, 4 bits wide

  assign out_3 = Dividend[3];
endmodule

module CRC (
  input  [7:0] in_1,
  input  [3:0] in_2,
  output [10:0] out_3
);

  wire [2:0] crc_divider_1_out_4, crc_divider_2_out_4, crc_divider_3_out_4, crc_divider_4_out_4,
       crc_divider_5_out_4, crc_divider_6_out_4, crc_divider_7_out_4;

  CRC__divider crc_divider_1 (.Dividend(in_1[7:4]), .Divisor(in_2), .out_4(crc_divider_1_out_4));  // open: out_3
  CRC__divider crc_divider_2 (
    .Dividend({crc_divider_1_out_4, in_1[3]}), .Divisor(in_2), .out_4(crc_divider_2_out_4));  // open: out_3
  CRC__divider crc_divider_3 (
    .Dividend({crc_divider_2_out_4, in_1[2]}), .Divisor(in_2), .out_4(crc_divider_3_out_4));  // open: out_3
  CRC__divider crc_divider_4 (
    .Dividend({crc_divider_3_out_4, in_1[1]}), .Divisor(in_2), .out_4(crc_divider_4_out_4));  // open: out_3
  CRC__divider crc_divider_5 (
    .Dividend({crc_divider_4_out_4, in_1[0]}), .Divisor(in_2), .out_4(crc_divider_5_out_4));  // open: out_3
  CRC__divider crc_divider_6 (
    .Dividend({crc_divider_5_out_4, 1'b0}), .Divisor(in_2), .out_4(crc_divider_6_out_4));  // open: out_3
  CRC__divider crc_divider_7 (
    .Dividend({crc_divider_6_out_4, 1'b0}), .Divisor(in_2), .out_4(crc_divider_7_out_4));  // open: out_3
  CRC__divider crc_divider_8 (
    .Dividend({crc_divider_7_out_4, 1'b0}), .Divisor(in_2), .out_4(out_3[2:0]));  // open: out_3

  assign out_3[10:3] = in_1;
endmodule

module main (
  input  in_1,
  output out_2,
  output out_3
);

  wire clock_1_out;
  wire [1:0] rom_1_data;
  wire [7:0] counter_1_q;

  Clock clock_1 (.out(clock_1_out));
  Counter counter_1 (.Q(counter_1_q), .clk(clock_1_out));  // open: load, D, count, carry, clr
  ROM #(.dataWidth(2)) rom_1 (.addr(counter_1_q), .data(rom_1_data));  // open: sel
  fsm fsm_1 (.In(rom_1_data), .CLR(in_1), .Z(out_2));

  // Notes on the sheet:
  //   contents of rom_1 (hex, n*v repeats v):
  //   4*1 4*2 4*3 1 2 1 3 1 2 2 0 1 0 0 0 1 1 2
endmodule

module _1GRF (
  input  [31:0] Input,
  input  Reset,
  input  Clock,
  input  Read0_enable,
  input  Read1_enable,
  input  Write_enable,
  output [31:0] Output_0,
  output [31:0] Output_1
);

  wire [31:0] register_1_q;

  Register #(.width(32)) register_1 (.D(Input), .en(Write_enable), .Q(register_1_q), .clk(Clock), .clr(Reset));
  assign Output_0 = Read0_enable ? register_1_q : 32'bz;  // Controlled_Buffer controlled_buffer_1
  assign Output_1 = Read1_enable ? register_1_q : 32'bz;  // Controlled_Buffer controlled_buffer_2
endmodule

module _2GRF (
  input  [31:0] Input,
  input  Read0_enable,
  input  Read0_address,
  input  Read1_enable,
  input  Clock,
  input  Reset,
  input  Read1_address,
  input  Write_enable,
  input  Write_address,
  output [31:0] Output_0,
  output [31:0] Output_1
);

  wire decoder_1_out0, decoder_1_out1, decoder_2_out0, decoder_2_out1, decoder_3_out0, decoder_3_out1;

  Decoder #(.disabled(0)) decoder_1 (
    .out0(decoder_1_out0), .out1(decoder_1_out1), .sel(Read0_address), .en(Read0_enable));
  Decoder #(.disabled(0)) decoder_2 (
    .out0(decoder_2_out0), .out1(decoder_2_out1), .sel(Read1_address), .en(Read1_enable));
  Decoder #(.disabled(0)) decoder_3 (
    .out0(decoder_3_out0), .out1(decoder_3_out1), .sel(Write_address), .en(Write_enable));
  _1GRF u_1grf_1 (
    .Input(Input), .Read0_enable(decoder_1_out0), .Read1_enable(decoder_2_out0),
    .Write_enable(decoder_3_out0), .Output_0(Output_0), .Output_1(Output_1), .Clock(Clock), .Reset(Reset));
  _1GRF u_1grf_2 (
    .Input(Input), .Read0_enable(decoder_1_out1), .Read1_enable(decoder_2_out1),
    .Write_enable(decoder_3_out1), .Output_0(Output_0), .Output_1(Output_1), .Clock(Clock), .Reset(Reset));
endmodule

module _4GRF (
  input  [31:0] Input,
  input  Read0_enable,
  input  [1:0] Read0_address,
  input  Read1_enable,
  input  Clock,
  input  Reset,
  input  [1:0] Read1_address,
  input  Write_enable,
  input  [1:0] Write_address,
  output [31:0] Output_0,
  output [31:0] Output_1
);

  wire decoder_1_out0, decoder_1_out1, decoder_2_out0, decoder_2_out1, decoder_3_out0, decoder_3_out1;

  Decoder #(.disabled(0)) decoder_1 (
    .out0(decoder_1_out0), .out1(decoder_1_out1), .sel(Read0_address[0]), .en(Read0_enable));
  Decoder #(.disabled(0)) decoder_2 (
    .out0(decoder_2_out0), .out1(decoder_2_out1), .sel(Read1_address[0]), .en(Read1_enable));
  Decoder #(.disabled(0)) decoder_3 (
    .out0(decoder_3_out0), .out1(decoder_3_out1), .sel(Write_address[0]), .en(Write_enable));
  _2GRF u_2grf_1 (
    .Input(Input), .Read0_enable(decoder_1_out0), .Read0_address(Read0_address[1]),
    .Read1_enable(decoder_2_out0), .Read1_address(Read1_address[1]), .Write_enable(decoder_3_out0),
    .Write_address(Write_address[1]), .Output_0(Output_0), .Output_1(Output_1), .Clock(Clock), .Reset(Reset));
  _2GRF u_2grf_2 (
    .Input(Input), .Read0_enable(decoder_1_out1), .Read0_address(Read0_address[1]),
    .Read1_enable(decoder_2_out1), .Read1_address(Read1_address[1]), .Write_enable(decoder_3_out1),
    .Write_address(Write_address[1]), .Output_0(Output_0), .Output_1(Output_1), .Clock(Clock), .Reset(Reset));
endmodule

module _8GRF (
  input  [31:0] Input,
  input  Read0_enable,
  input  [2:0] Read0_address,
  input  Read1_enable,
  input  Clock,
  input  Reset,
  input  [2:0] Read1_address,
  input  Write_enable,
  input  [2:0] Write_address,
  output [31:0] Output_0,
  output [31:0] Output_1
);

  wire decoder_1_out0, decoder_1_out1, decoder_2_out0, decoder_2_out1, decoder_3_out0, decoder_3_out1;

  Decoder #(.disabled(0)) decoder_1 (
    .out0(decoder_1_out0), .out1(decoder_1_out1), .sel(Read0_address[0]), .en(Read0_enable));
  Decoder #(.disabled(0)) decoder_2 (
    .out0(decoder_2_out0), .out1(decoder_2_out1), .sel(Read1_address[0]), .en(Read1_enable));
  Decoder #(.disabled(0)) decoder_3 (
    .out0(decoder_3_out0), .out1(decoder_3_out1), .sel(Write_address[0]), .en(Write_enable));
  _4GRF u_4grf_1 (
    .Input(Input), .Read0_enable(decoder_1_out0), .Read0_address(Read0_address[2:1]),
    .Read1_enable(decoder_2_out0), .Read1_address(Read1_address[2:1]), .Write_enable(decoder_3_out0),
    .Write_address(Write_address[2:1]), .Output_0(Output_0), .Output_1(Output_1), .Clock(Clock), .Reset(Reset));
  _4GRF u_4grf_2 (
    .Input(Input), .Read0_enable(decoder_1_out1), .Read0_address(Read0_address[2:1]),
    .Read1_enable(decoder_2_out1), .Read1_address(Read1_address[2:1]), .Write_enable(decoder_3_out1),
    .Write_address(Write_address[2:1]), .Output_0(Output_0), .Output_1(Output_1), .Clock(Clock), .Reset(Reset));
endmodule

module _16GRF (
  input  [31:0] Input,
  input  Read0_enable,
  input  [3:0] Read0_address,
  input  Read1_enable,
  input  Clock,
  input  Reset,
  input  [3:0] Read1_address,
  input  Write_enable,
  input  [3:0] Write_address,
  output [31:0] Output_0,
  output [31:0] Output_1
);

  wire decoder_1_out0, decoder_1_out1, decoder_2_out0, decoder_2_out1, decoder_3_out0, decoder_3_out1;

  Decoder #(.disabled(0)) decoder_1 (
    .out0(decoder_1_out0), .out1(decoder_1_out1), .sel(Read0_address[0]), .en(Read0_enable));
  Decoder #(.disabled(0)) decoder_2 (
    .out0(decoder_2_out0), .out1(decoder_2_out1), .sel(Read1_address[0]), .en(Read1_enable));
  Decoder #(.disabled(0)) decoder_3 (
    .out0(decoder_3_out0), .out1(decoder_3_out1), .sel(Write_address[0]), .en(Write_enable));
  _8GRF u_8grf_1 (
    .Input(Input), .Read0_enable(decoder_1_out0), .Read0_address(Read0_address[3:1]),
    .Read1_enable(decoder_2_out0), .Read1_address(Read1_address[3:1]), .Write_enable(decoder_3_out0),
    .Write_address(Write_address[3:1]), .Output_0(Output_0), .Output_1(Output_1), .Clock(Clock), .Reset(Reset));
  _8GRF u_8grf_2 (
    .Input(Input), .Read0_enable(decoder_1_out1), .Read0_address(Read0_address[3:1]),
    .Read1_enable(decoder_2_out1), .Read1_address(Read1_address[3:1]), .Write_enable(decoder_3_out1),
    .Write_address(Write_address[3:1]), .Output_0(Output_0), .Output_1(Output_1), .Clock(Clock), .Reset(Reset));
endmodule

module GRF__helper (
  input  Enable,
  input  [4:0] addr,
  output _0_enable,
  output _1_enable,
  output _2_enable,
  output _4_enable,
  output _8_enable,
  output _16_enable,
  output _2_addr,
  output [1:0] _4_addr,
  output [2:0] _8_addr,
  output [3:0] _16_addr
);

  wire nor_1_out, nor_2_out, nor_3_out, nor_4_out, nor_5_out;

  nor nor_1 (nor_1_out, addr[0], addr[1], addr[2], addr[3], addr[4]);
  nor nor_2 (nor_2_out, addr[1], addr[2], addr[3], addr[4]);
  nor nor_3 (nor_3_out, addr[2], addr[3], addr[4]);
  nor nor_4 (nor_4_out, addr[3], addr[4]);
  nor nor_5 (nor_5_out, addr[4], addr[4]);
  and and_1 (_0_enable, Enable, nor_1_out);
  and and_2 (_1_enable, Enable, nor_2_out, addr[0]);
  and and_3 (_2_enable, Enable, nor_3_out, addr[1]);
  and and_4 (_4_enable, Enable, nor_4_out, addr[2]);
  and and_5 (_8_enable, Enable, nor_5_out, addr[3]);
  and and_6 (_16_enable, Enable, addr[4]);

  assign _2_addr = addr[0];
  assign _4_addr = addr[1:0];
  assign _8_addr = addr[2:0];
  assign _16_addr = addr[3:0];

  // Notes on the sheet:
  //   Enable: pull=up
endmodule

module GRF (
  input  [31:0] Input,
  input  [4:0] Read0_address,
  input  [4:0] Read1_address,
  input  Write_enable,
  input  [4:0] Write_address,
  input  Reset,
  input  Clock,
  output [31:0] Output_0,
  output [31:0] Output_1
);

  wire grf_helper_1__1_enable, grf_helper_1__2_addr, grf_helper_1__2_enable, grf_helper_1__4_enable,
       grf_helper_1__8_enable, grf_helper_1__16_enable, grf_helper_2__0_enable, grf_helper_2__1_enable,
       grf_helper_2__2_addr, grf_helper_2__2_enable, grf_helper_2__4_enable, grf_helper_2__8_enable,
       grf_helper_2__16_enable, grf_helper_3__0_enable, grf_helper_3__1_enable, grf_helper_3__2_addr,
       grf_helper_3__2_enable, grf_helper_3__4_enable, grf_helper_3__8_enable, grf_helper_3__16_enable;
  wire [1:0] grf_helper_1__4_addr, grf_helper_2__4_addr, grf_helper_3__4_addr;
  wire [2:0] grf_helper_1__8_addr, grf_helper_2__8_addr, grf_helper_3__8_addr;
  wire [3:0] grf_helper_1__16_addr, grf_helper_2__16_addr, grf_helper_3__16_addr;

  GRF__helper grf_helper_1 (
    .addr(Write_address), ._1_enable(grf_helper_1__1_enable), ._2_enable(grf_helper_1__2_enable),
    ._4_enable(grf_helper_1__4_enable), ._8_enable(grf_helper_1__8_enable),
    ._16_enable(grf_helper_1__16_enable), ._2_addr(grf_helper_1__2_addr), ._4_addr(grf_helper_1__4_addr),
    ._8_addr(grf_helper_1__8_addr), ._16_addr(grf_helper_1__16_addr), .Enable(Write_enable));  // open: _0_enable
  GRF__helper grf_helper_2 (
    .addr(Read0_address), ._0_enable(grf_helper_2__0_enable), ._1_enable(grf_helper_2__1_enable),
    ._2_enable(grf_helper_2__2_enable), ._4_enable(grf_helper_2__4_enable),
    ._8_enable(grf_helper_2__8_enable), ._16_enable(grf_helper_2__16_enable), ._2_addr(grf_helper_2__2_addr),
    ._4_addr(grf_helper_2__4_addr), ._8_addr(grf_helper_2__8_addr), ._16_addr(grf_helper_2__16_addr));  // open: Enable
  GRF__helper grf_helper_3 (
    .addr(Read1_address), ._0_enable(grf_helper_3__0_enable), ._1_enable(grf_helper_3__1_enable),
    ._2_enable(grf_helper_3__2_enable), ._4_enable(grf_helper_3__4_enable),
    ._8_enable(grf_helper_3__8_enable), ._16_enable(grf_helper_3__16_enable), ._2_addr(grf_helper_3__2_addr),
    ._4_addr(grf_helper_3__4_addr), ._8_addr(grf_helper_3__8_addr), ._16_addr(grf_helper_3__16_addr));  // open: Enable
  _1GRF u_1grf_1 (
    .Read0_enable(grf_helper_2__0_enable), .Read1_enable(grf_helper_3__0_enable), .Output_0(Output_0),
    .Output_1(Output_1));  // open: Input, Write_enable, Clock, Reset
  _1GRF u_1grf_2 (
    .Input(Input), .Read0_enable(grf_helper_2__1_enable), .Read1_enable(grf_helper_3__1_enable),
    .Write_enable(grf_helper_1__1_enable), .Output_0(Output_0), .Output_1(Output_1), .Clock(Clock),
    .Reset(Reset));
  _2GRF u_2grf_1 (
    .Input(Input), .Read0_enable(grf_helper_2__2_enable), .Read0_address(grf_helper_2__2_addr),
    .Read1_enable(grf_helper_3__2_enable), .Read1_address(grf_helper_3__2_addr),
    .Write_enable(grf_helper_1__2_enable), .Write_address(grf_helper_1__2_addr), .Output_0(Output_0),
    .Output_1(Output_1), .Clock(Clock), .Reset(Reset));
  _4GRF u_4grf_1 (
    .Input(Input), .Read0_enable(grf_helper_2__4_enable), .Read0_address(grf_helper_2__4_addr),
    .Read1_enable(grf_helper_3__4_enable), .Read1_address(grf_helper_3__4_addr),
    .Write_enable(grf_helper_1__4_enable), .Write_address(grf_helper_1__4_addr), .Output_0(Output_0),
    .Output_1(Output_1), .Clock(Clock), .Reset(Reset));
  _8GRF u_8grf_1 (
    .Input(Input), .Read0_enable(grf_helper_2__8_enable), .Read0_address(grf_helper_2__8_addr),
    .Read1_enable(grf_helper_3__8_enable), .Read1_address(grf_helper_3__8_addr),
    .Write_enable(grf_helper_1__8_enable), .Write_address(grf_helper_1__8_addr), .Output_0(Output_0),
    .Output_1(Output_1), .Clock(Clock), .Reset(Reset));
  _16GRF u_16grf_1 (
    .Input(Input), .Read0_enable(grf_helper_2__16_enable), .Read0_address(grf_helper_2__16_addr),
    .Read1_enable(grf_helper_3__16_enable), .Read1_address(grf_helper_3__16_addr),
    .Write_enable(grf_helper_1__16_enable), .Write_address(grf_helper_1__16_addr), .Output_0(Output_0),
    .Output_1(Output_1), .Clock(Clock), .Reset(Reset));
endmodule

module GRF2 (
  input  [31:0] Input,
  input  [4:0] read_addr0,
  input  [4:0] read_addr1,
  input  write_enable,
  input  [4:0] write_addr,
  input  Clock,
  output [31:0] out_7,
  output [31:0] out_8
);

  wire decoder_1_out0, decoder_1_out1, decoder_1_out2, decoder_1_out3, decoder_1_out4, decoder_1_out5,
       decoder_1_out6, decoder_1_out7, decoder_1_out8, decoder_1_out9, decoder_1_out10, decoder_1_out11,
       decoder_1_out12, decoder_1_out13, decoder_1_out14, decoder_1_out15, decoder_1_out16, decoder_1_out17,
       decoder_1_out18, decoder_1_out19, decoder_1_out20, decoder_1_out21, decoder_1_out22, decoder_1_out23,
       decoder_1_out24, decoder_1_out25, decoder_1_out26, decoder_1_out27, decoder_1_out28, decoder_1_out29,
       decoder_1_out30, decoder_1_out31;
  wire [31:0] register_1_q, register_2_q, register_3_q, register_4_q, register_5_q, register_6_q,
       register_7_q, register_8_q, register_9_q, register_10_q, register_11_q, register_12_q, register_13_q,
       register_14_q, register_15_q, register_16_q, register_17_q, register_18_q, register_19_q,
       register_20_q, register_21_q, register_22_q, register_23_q, register_24_q, register_25_q,
       register_26_q, register_27_q, register_28_q, register_29_q, register_30_q, register_31_q,
       register_32_q;

  Decoder #(.select(5), .disabled(0)) decoder_1 (
    .out0(decoder_1_out0), .out1(decoder_1_out1), .out2(decoder_1_out2), .out3(decoder_1_out3),
    .out4(decoder_1_out4), .out5(decoder_1_out5), .out6(decoder_1_out6), .out7(decoder_1_out7),
    .out8(decoder_1_out8), .out9(decoder_1_out9), .out10(decoder_1_out10), .out11(decoder_1_out11),
    .out12(decoder_1_out12), .out13(decoder_1_out13), .out14(decoder_1_out14), .out15(decoder_1_out15),
    .out16(decoder_1_out16), .out17(decoder_1_out17), .out18(decoder_1_out18), .out19(decoder_1_out19),
    .out20(decoder_1_out20), .out21(decoder_1_out21), .out22(decoder_1_out22), .out23(decoder_1_out23),
    .out24(decoder_1_out24), .out25(decoder_1_out25), .out26(decoder_1_out26), .out27(decoder_1_out27),
    .out28(decoder_1_out28), .out29(decoder_1_out29), .out30(decoder_1_out30), .out31(decoder_1_out31),
    .sel(write_addr), .en(write_enable));
  Register #(.width(32)) register_1 (.en(decoder_1_out0), .Q(register_1_q), .clk(Clock));  // open: D, clr
  Register #(.width(32)) register_2 (.D(Input), .en(decoder_1_out1), .Q(register_2_q), .clk(Clock));  // open: clr
  Register #(.width(32)) register_3 (.D(Input), .en(decoder_1_out2), .Q(register_3_q), .clk(Clock));  // open: clr
  Register #(.width(32)) register_4 (.D(Input), .en(decoder_1_out3), .Q(register_4_q), .clk(Clock));  // open: clr
  Register #(.width(32)) register_5 (.D(Input), .en(decoder_1_out4), .Q(register_5_q), .clk(Clock));  // open: clr
  Register #(.width(32)) register_6 (.D(Input), .en(decoder_1_out5), .Q(register_6_q), .clk(Clock));  // open: clr
  Register #(.width(32)) register_7 (.D(Input), .en(decoder_1_out6), .Q(register_7_q), .clk(Clock));  // open: clr
  Register #(.width(32)) register_8 (.D(Input), .en(decoder_1_out7), .Q(register_8_q), .clk(Clock));  // open: clr
  Register #(.width(32)) register_9 (.D(Input), .en(decoder_1_out8), .Q(register_9_q), .clk(Clock));  // open: clr
  Register #(.width(32)) register_10 (.D(Input), .en(decoder_1_out9), .Q(register_10_q), .clk(Clock));  // open: clr
  Register #(.width(32)) register_11 (.D(Input), .en(decoder_1_out10), .Q(register_11_q), .clk(Clock));  // open: clr
  Register #(.width(32)) register_12 (.D(Input), .en(decoder_1_out11), .Q(register_12_q), .clk(Clock));  // open: clr
  Register #(.width(32)) register_13 (.D(Input), .en(decoder_1_out12), .Q(register_13_q), .clk(Clock));  // open: clr
  Register #(.width(32)) register_14 (.D(Input), .en(decoder_1_out13), .Q(register_14_q), .clk(Clock));  // open: clr
  Register #(.width(32)) register_15 (.D(Input), .en(decoder_1_out14), .Q(register_15_q), .clk(Clock));  // open: clr
  Register #(.width(32)) register_16 (.D(Input), .en(decoder_1_out15), .Q(register_16_q), .clk(Clock));  // open: clr
  Register #(.width(32)) register_17 (.D(Input), .en(decoder_1_out16), .Q(register_17_q), .clk(Clock));  // open: clr
  Register #(.width(32)) register_18 (.D(Input), .en(decoder_1_out17), .Q(register_18_q), .clk(Clock));  // open: clr
  Register #(.width(32)) register_19 (.D(Input), .en(decoder_1_out18), .Q(register_19_q), .clk(Clock));  // open: clr
  Register #(.width(32)) register_20 (.D(Input), .en(decoder_1_out19), .Q(register_20_q), .clk(Clock));  // open: clr
  Register #(.width(32)) register_21 (.D(Input), .en(decoder_1_out20), .Q(register_21_q), .clk(Clock));  // open: clr
  Register #(.width(32)) register_22 (.D(Input), .en(decoder_1_out21), .Q(register_22_q), .clk(Clock));  // open: clr
  Register #(.width(32)) register_23 (.D(Input), .en(decoder_1_out22), .Q(register_23_q), .clk(Clock));  // open: clr
  Register #(.width(32)) register_24 (.D(Input), .en(decoder_1_out23), .Q(register_24_q), .clk(Clock));  // open: clr
  Register #(.width(32)) register_25 (.D(Input), .en(decoder_1_out24), .Q(register_25_q), .clk(Clock));  // open: clr
  Register #(.width(32)) register_26 (.D(Input), .en(decoder_1_out25), .Q(register_26_q), .clk(Clock));  // open: clr
  Register #(.width(32)) register_27 (.D(Input), .en(decoder_1_out26), .Q(register_27_q), .clk(Clock));  // open: clr
  Register #(.width(32)) register_28 (.D(Input), .en(decoder_1_out27), .Q(register_28_q), .clk(Clock));  // open: clr
  Register #(.width(32)) register_29 (.D(Input), .en(decoder_1_out28), .Q(register_29_q), .clk(Clock));  // open: clr
  Register #(.width(32)) register_30 (.D(Input), .en(decoder_1_out29), .Q(register_30_q), .clk(Clock));  // open: clr
  Register #(.width(32)) register_31 (.D(Input), .en(decoder_1_out30), .Q(register_31_q), .clk(Clock));  // open: clr
  Register #(.width(32)) register_32 (.D(Input), .en(decoder_1_out31), .Q(register_32_q), .clk(Clock));  // open: clr
  Multiplexer #(.select(5), .width(32)) multiplexer_1 (
    .in0(register_1_q), .in1(register_2_q), .in2(register_3_q), .in3(register_4_q), .in4(register_5_q),
    .in5(register_6_q), .in6(register_7_q), .in7(register_8_q), .in8(register_9_q), .in9(register_10_q),
    .in10(register_11_q), .in11(register_12_q), .in12(register_13_q), .in13(register_14_q),
    .in14(register_15_q), .in15(register_16_q), .in16(register_17_q), .in17(register_18_q),
    .in18(register_19_q), .in19(register_20_q), .in20(register_21_q), .in21(register_22_q),
    .in22(register_23_q), .in23(register_24_q), .in24(register_25_q), .in25(register_26_q),
    .in26(register_27_q), .in27(register_28_q), .in28(register_29_q), .in29(register_30_q),
    .in30(register_31_q), .in31(register_32_q), .out(out_7), .sel(read_addr0));  // open: en
  Multiplexer #(.select(5), .width(32)) multiplexer_2 (
    .in0(register_1_q), .in1(register_2_q), .in2(register_3_q), .in3(register_4_q), .in4(register_5_q),
    .in5(register_6_q), .in6(register_7_q), .in7(register_8_q), .in8(register_9_q), .in9(register_10_q),
    .in10(register_11_q), .in11(register_12_q), .in12(register_13_q), .in13(register_14_q),
    .in14(register_15_q), .in15(register_16_q), .in16(register_17_q), .in17(register_18_q),
    .in18(register_19_q), .in19(register_20_q), .in20(register_21_q), .in21(register_22_q),
    .in22(register_23_q), .in23(register_24_q), .in24(register_25_q), .in25(register_26_q),
    .in26(register_27_q), .in27(register_28_q), .in28(register_29_q), .in29(register_30_q),
    .in30(register_31_q), .in31(register_32_q), .out(out_8), .sel(read_addr1));  // open: en
endmodule

module GRF_pack (
  input  in_1,
  input  in_2,
  input  in_3,
  input  [4:0] in_4,
  input  [4:0] in_5,
  input  [4:0] in_6,
  input  [31:0] in_7,
  output [31:0] out_8,
  output [31:0] out_9
);

  GRF grf_1 (
    .Input(in_7), .Read0_address(in_4), .Read1_address(in_5), .Write_enable(in_3), .Write_address(in_6),
    .Output_0(out_8), .Output_1(out_9), .Clock(in_1), .Reset(in_2));
endmodule

module ftoi (
  input  [15:0] in_1,
  output [31:0] out_2
);

  wire and_1_out, or_2_out, subtractor_1_bout, subtractor_2_bout;
  wire [4:0] negator_1_out, subtractor_1_out, subtractor_2_out;
  wire [10:10] or_1_out;
  wire [31:0] bit_extender_1_out, multiplexer_1_out, multiplexer_3_out, negator_2_out, shifter_1_out,
       shifter_2_out;

  or or_1 (or_1_out[10], in_1[10], in_1[11], in_1[12], in_1[13], in_1[14]);
  and and_1 (and_1_out, in_1[10], in_1[11], in_1[12], in_1[13], in_1[14]);
  Subtractor #(.width(5)) subtractor_1 (
    .a(in_1[14:10]), .b(5'b01111), .out(subtractor_1_out), .bout(subtractor_1_bout));  // open: bin
  assign bit_extender_1_out = {{21{1'b0}}, {or_1_out[10], in_1[9:0]}};  // Bit_Extender bit_extender_1
  or or_2 (or_2_out, and_1_out, subtractor_1_bout);
  Subtractor #(.width(5)) subtractor_2 (
    .a(subtractor_1_out), .b(5'b01010), .out(subtractor_2_out), .bout(subtractor_2_bout));  // open: bin
  Shifter #(.width(32)) shifter_1 (.in(bit_extender_1_out), .\dist (subtractor_2_out), .out(shifter_1_out));
  Shifter #(.width(32), .shift("lr")) shifter_2 (.in(bit_extender_1_out), .\dist (negator_1_out), .out(shifter_2_out));
  Negator #(.width(5)) negator_1 (.in(subtractor_2_out), .out(negator_1_out));
  Multiplexer #(.width(32), .enable("false")) multiplexer_1 (
    .in0(shifter_1_out), .in1(shifter_2_out), .out(multiplexer_1_out), .sel(subtractor_2_bout));
  Negator #(.width(32)) negator_2 (.in(multiplexer_1_out), .out(negator_2_out));
  Multiplexer #(.width(32), .enable("false")) multiplexer_2 (
    .in0(multiplexer_3_out), .in1({32{1'b0}}), .out(out_2), .sel(or_2_out));
  Multiplexer #(.width(32), .enable("false")) multiplexer_3 (
    .in0(multiplexer_1_out), .in1(negator_2_out), .out(multiplexer_3_out), .sel(in_1[15]));
endmodule

module navigation__location_next (
  input  [1:0] R,
  input  [1:0] Dir,
  output [1:0] out_3,
  output hit,
  output arrive
);

  wire and_1_out, and_2_out, and_3_out, and_4_out, and_5_out, and_6_out, and_7_out, and_8_out, and_9_out,
       and_10_out, and_11_out, and_12_out, and_13_out, and_14_out, and_15_out, and_16_out, and_17_out,
       not_1_out, not_2_out, not_3_out, not_4_out, not_5_out, not_6_out, not_7_out, not_8_out, not_9_out,
       not_10_out, not_11_out, not_12_out, not_13_out, not_14_out, not_15_out, not_16_out, not_17_out,
       not_18_out, not_19_out, not_20_out, not_21_out, not_22_out, not_23_out, not_24_out, not_25_out,
       not_26_out, not_27_out, not_28_out;

  not not_1 (not_1_out, R[0]);
  not not_2 (not_2_out, Dir[1]);
  not not_3 (not_3_out, Dir[0]);
  not not_4 (not_4_out, R[0]);
  not not_5 (not_5_out, Dir[0]);
  not not_6 (not_6_out, R[1]);
  not not_7 (not_7_out, R[0]);
  not not_8 (not_8_out, Dir[1]);
  not not_9 (not_9_out, Dir[0]);
  not not_10 (not_10_out, R[0]);
  not not_11 (not_11_out, Dir[1]);
  not not_12 (not_12_out, Dir[0]);
  not not_13 (not_13_out, Dir[1]);
  not not_14 (not_14_out, Dir[0]);
  not not_15 (not_15_out, R[0]);
  not not_16 (not_16_out, Dir[1]);
  not not_17 (not_17_out, Dir[1]);
  not not_18 (not_18_out, Dir[0]);
  not not_19 (not_19_out, R[1]);
  and and_1 (and_1_out, not_19_out, R[0], not_20_out);
  not not_20 (not_20_out, Dir[1]);
  not not_21 (not_21_out, Dir[1]);
  and and_2 (and_2_out, R[0], not_21_out, Dir[0]);
  and and_3 (and_3_out, R[1], not_1_out, not_2_out, not_3_out);
  and and_4 (and_4_out, R[1], not_4_out, Dir[1], Dir[0]);
  and and_5 (and_5_out, R[1], R[0], Dir[1], not_5_out);
  and and_6 (and_6_out, not_6_out, not_7_out, not_8_out, not_9_out);
  and and_7 (and_7_out, R[0], Dir[0]);
  and and_8 (and_8_out, R[1], Dir[1], not_22_out);
  not not_22 (not_22_out, Dir[0]);
  not not_23 (not_23_out, R[1]);
  and and_9 (and_9_out, not_23_out, not_24_out, Dir[0]);
  not not_24 (not_24_out, R[0]);
  not not_25 (not_25_out, R[1]);
  and and_10 (and_10_out, not_25_out, not_26_out, Dir[1]);
  not not_26 (not_26_out, R[0]);
  not not_27 (not_27_out, R[1]);
  and and_11 (and_11_out, not_27_out, Dir[1], Dir[0]);
  not not_28 (not_28_out, R[0]);
  and and_12 (and_12_out, not_28_out, Dir[1], Dir[0]);
  and and_13 (and_13_out, R[1], not_10_out, not_11_out, not_12_out);
  and and_14 (and_14_out, R[1], R[0], not_13_out, Dir[0]);
  and and_15 (and_15_out, R[1], R[0], Dir[1], not_14_out);
  and and_16 (and_16_out, R[1], not_15_out, not_16_out, Dir[0]);
  and and_17 (and_17_out, R[1], R[0], not_17_out, not_18_out);
  or or_1 (out_3[1], and_1_out, and_2_out, and_3_out, and_4_out, and_5_out);
  or or_2 (out_3[0], and_6_out, and_7_out, and_8_out);
  or or_3 (arrive, and_16_out, and_17_out);
  or or_4 (hit, and_9_out, and_10_out, and_11_out, and_12_out, and_13_out, and_14_out, and_15_out);
endmodule

module navigation (
  input  [1:0] dir,
  input  clk,
  input  reset,
  output arrive,
  output hit
);

  wire and_1_out, clock_1_out, navigation_location_next_1_arrive, navigation_location_next_1_hit, not_1_out,
       or_1_out, or_2_out;
  wire [1:0] navigation_location_next_1_out_3, register_1_q;

  Clock clock_1 (.out(clock_1_out));
  or or_1 (or_1_out, clk, clock_1_out);
  and and_1 (and_1_out, or_1_out, arrive);
  or or_2 (or_2_out, and_1_out, reset);
  Register #(.width(2)) register_1 (
    .D(navigation_location_next_1_out_3), .en(not_1_out), .Q(register_1_q), .clk(or_1_out), .clr(or_2_out));
  not not_1 (not_1_out, navigation_location_next_1_arrive);
  navigation__location_next navigation_location_next_1 (
    .R(register_1_q), .Dir(dir), .out_3(navigation_location_next_1_out_3),
    .hit(navigation_location_next_1_hit), .arrive(navigation_location_next_1_arrive));
  Register #(.width(1)) register_2 (
    .D(navigation_location_next_1_arrive), .Q(arrive), .clk(or_1_out), .clr(reset));  // open: en
  Register #(.width(1)) register_3 (
    .D(navigation_location_next_1_hit), .Q(hit), .clk(or_1_out), .clr(or_2_out));  // open: en
endmodule

module fsm__next_state_logic (
  input  i1,
  input  i0,
  input  d1,
  input  d0,
  output n1,
  output n0
);

  wire and_1_out, and_2_out, and_3_out, and_4_out, and_5_out, and_6_out, and_7_out, and_8_out, not_1_out,
       not_2_out, not_3_out, not_4_out, not_5_out, not_6_out, not_7_out, not_8_out, not_9_out, not_10_out,
       not_11_out, not_12_out, not_13_out, not_14_out, not_15_out, not_16_out;

  not not_1 (not_1_out, i1);
  and and_1 (and_1_out, not_1_out, i0, not_2_out);
  not not_2 (not_2_out, d1);
  not not_3 (not_3_out, i1);
  and and_2 (and_2_out, not_3_out, i0, not_4_out);
  not not_4 (not_4_out, d0);
  not not_5 (not_5_out, i0);
  and and_3 (and_3_out, i1, not_5_out, not_6_out);
  not not_6 (not_6_out, d1);
  and and_4 (and_4_out, i1, not_7_out, not_8_out);
  not not_7 (not_7_out, i0);
  not not_8 (not_8_out, d0);
  not not_9 (not_9_out, i1);
  not not_10 (not_10_out, i0);
  not not_11 (not_11_out, d1);
  not not_12 (not_12_out, i1);
  not not_13 (not_13_out, d0);
  not not_14 (not_14_out, i0);
  not not_15 (not_15_out, d0);
  not not_16 (not_16_out, d1);
  or or_1 (n1, and_1_out, and_2_out, and_3_out, and_4_out);
  and and_5 (and_5_out, not_9_out, not_10_out, not_11_out, d0);
  and and_6 (and_6_out, not_12_out, i0, not_13_out);
  and and_7 (and_7_out, i1, not_14_out, not_15_out);
  and and_8 (and_8_out, i1, i0, not_16_out, d0);
  or or_2 (n0, and_5_out, and_6_out, and_7_out, and_8_out);
endmodule

module fsm__output_logic (
  input  i1,
  input  i0,
  input  d1,
  input  d0,
  output z
);

  wire not_1_out;

  not not_1 (not_1_out, d0);
  and and_1 (z, i1, i0, not_1_out);
endmodule

module fsm (
  input  [1:0] In,
  input  CLR,
  output Z
);

  wire and_1_out, and_2_out, clock_1_out, fsm_next_state_logic_1_n0, fsm_next_state_logic_1_n1, not_1_out,
       register_1_q, register_2_q;

  Clock clock_1 (.out(clock_1_out));
  not not_1 (not_1_out, CLR);
  fsm__next_state_logic fsm_next_state_logic_1 (
    .i1(register_1_q), .i0(register_2_q), .d1(In[1]), .d0(In[0]), .n1(fsm_next_state_logic_1_n1),
    .n0(fsm_next_state_logic_1_n0));
  and and_1 (and_1_out, not_1_out, fsm_next_state_logic_1_n1);
  Register #(.width(1)) register_1 (.D(and_1_out), .Q(register_1_q), .clk(clock_1_out));  // open: en, clr
  and and_2 (and_2_out, fsm_next_state_logic_1_n0, not_1_out);
  Register #(.width(1)) register_2 (.D(and_2_out), .Q(register_2_q), .clk(clock_1_out));  // open: en, clr
  fsm__output_logic fsm_output_logic_1 (.i1(register_1_q), .i0(register_2_q), .d1(In[1]), .d0(In[0]), .z(Z));
endmodule
