// Logisim project ALU.circ as structural Verilog: 21 circuits, main circuit ALU
module ALU (
  input  [3:0] funct,
  input  [31:0] A,
  input  [31:0] B,
  input  [4:0] shift,
  input  signed_compare,
  output [31:0] S,
  output overflow,
  output gt,
  output zero,
  output eq,
  output lt
);

  wire alu_control_1_sub;
  wire [1:0] alu_control_1_logic_control, alu_control_1_result_select;
  wire [2:0] alu_control_1_shift_control;
  wire [31:0] arithmetic, \logic , shift_t;

  ALU__control alu_control_1 (
    .funct(funct), .result_select(alu_control_1_result_select), .sub(alu_control_1_sub),
    .logic_control(alu_control_1_logic_control), .shift_control(alu_control_1_shift_control));
  ALU__logic alu_logic_1 (.A(A), .B(B), .Res(\logic ), .control(alu_control_1_logic_control));
  ALU__arithmetic alu_arithmetic_1 (.A(A), .B(B), .S(arithmetic), .sub(alu_control_1_sub), .overflow(overflow));
  _32bit_comparer u_32bit_comparer_1 (.A(A), .B(B), .gt(gt), .eq(eq), .lt(lt), .\signed (signed_compare));
  ALU__shifter alu_shifter_1 (.A(A), .B(shift), .S(shift_t), .control(alu_control_1_shift_control));
  Multiplexer #(.select(2), .width(32), .enable("false")) multiplexer_1 (
    .in0(\logic ), .in1(arithmetic), .in2(shift_t), .out(S), .sel(alu_control_1_result_select));  // open: in3
  nor nor_1 (zero, S[0], S[1], S[2], S[3], S[4], S[5], S[6], S[7], S[8], S[9], S[10], S[11], S[12], S[13], S[14], S[15], S[17], S[18], S[19], S[20], S[21], S[22], S[23], S[24], S[25], S[26], S[27], S[28], S[29], S[30], S[31], S[16]);

  // Other names for the same wires on the sheet: shift_width[4:0] = shift
endmodule

module _4_bit_adder__raw (
  input  Cin,
  input  A0,
  input  A1,
  input  A2,
  input  A3,
  input  B0,
  input  B1,
  input  B2,
  input  B3,
  output Cout,
  output R0,
  output R1,
  output R2,
  output R3,
  output overflow
);

  wire and_1_out, and_2_out, and_3_out, and_4_out, and_5_out, and_6_out, and_7_out, and_8_out, and_9_out,
       and_10_out, and_11_out, and_12_out, and_13_out, and_14_out, and_15_out, and_16_out, and_17_out,
       and_18_out, and_19_out, and_20_out, and_21_out, and_22_out, and_23_out, and_24_out, and_25_out,
       and_26_out, and_27_out, and_28_out, and_29_out, and_30_out, and_31_out, and_32_out, and_33_out,
       and_34_out, and_35_out, and_36_out, and_37_out, and_38_out, and_39_out, and_40_out, and_41_out,
       and_42_out, and_43_out, and_44_out, and_45_out, and_46_out, and_47_out, and_48_out, and_49_out,
       and_50_out, and_51_out, and_52_out, and_53_out, and_54_out, and_55_out, and_56_out, and_57_out,
       and_58_out, and_59_out, and_60_out, and_61_out, and_62_out, and_63_out, and_64_out, and_65_out,
       and_66_out, and_67_out, and_68_out, and_69_out, and_70_out, and_71_out, and_72_out, and_73_out,
       and_74_out, and_75_out, and_76_out, and_77_out, and_78_out, and_79_out, and_80_out, and_81_out,
       and_82_out, and_83_out, and_84_out, and_85_out, and_86_out, and_87_out, and_88_out, and_89_out,
       and_90_out, and_91_out, and_92_out, and_93_out, and_94_out, and_95_out, and_96_out, and_97_out,
       and_98_out, and_99_out, and_100_out, and_101_out, and_102_out, and_103_out, and_104_out, and_105_out,
       and_106_out, and_107_out, and_108_out, and_109_out, and_110_out, and_111_out, and_112_out,
       and_113_out, and_114_out, and_115_out, and_116_out, and_117_out, and_118_out, and_119_out,
       and_120_out, and_121_out, and_122_out, and_123_out, and_124_out, and_125_out, and_126_out,
       and_127_out, and_128_out, and_129_out, and_130_out, and_131_out, and_132_out, and_133_out,
       and_134_out, and_135_out, and_136_out, not_1_out, not_2_out, not_3_out, not_4_out, not_5_out,
       not_6_out, not_7_out, not_8_out, not_9_out, not_10_out, not_11_out, not_12_out, not_13_out,
       not_14_out, not_15_out, not_16_out, not_17_out, not_18_out, not_19_out, not_20_out, not_21_out,
       not_22_out, not_23_out, not_24_out, not_25_out, not_26_out, not_27_out, not_28_out, not_29_out,
       not_30_out, not_31_out, not_32_out, not_33_out, not_34_out, not_35_out, not_36_out, not_37_out,
       not_38_out, not_39_out, not_40_out, not_41_out, not_42_out, not_43_out, not_44_out, not_45_out,
       not_46_out, not_47_out, not_48_out, not_49_out, not_50_out, not_51_out, not_52_out, not_53_out,
       not_54_out, not_55_out, not_56_out, not_57_out, not_58_out, not_59_out, not_60_out, not_61_out,
       not_62_out, not_63_out, not_64_out, not_65_out, not_66_out, not_67_out, not_68_out, not_69_out,
       not_70_out, not_71_out, not_72_out, not_73_out, not_74_out, not_75_out, not_76_out, not_77_out,
       not_78_out, not_79_out, not_80_out, not_81_out, not_82_out, not_83_out, not_84_out, not_85_out,
       not_86_out, not_87_out, not_88_out, not_89_out, not_90_out, not_91_out, not_92_out, not_93_out,
       not_94_out, not_95_out, not_96_out, not_97_out, not_98_out, not_99_out, not_100_out, not_101_out,
       not_102_out, not_103_out, not_104_out, not_105_out, not_106_out, not_107_out, not_108_out,
       not_109_out, not_110_out, not_111_out, not_112_out, not_113_out, not_114_out, not_115_out,
       not_116_out, not_117_out, not_118_out, not_119_out, not_120_out, not_121_out, not_122_out,
       not_123_out, not_124_out, not_125_out, not_126_out, not_127_out, not_128_out, not_129_out,
       not_130_out, not_131_out, not_132_out, not_133_out, not_134_out, not_135_out, not_136_out,
       not_137_out, not_138_out, not_139_out, not_140_out, not_141_out, not_142_out, not_143_out,
       not_144_out, not_145_out, not_146_out, not_147_out, not_148_out, not_149_out, not_150_out,
       not_151_out, not_152_out, not_153_out, not_154_out, not_155_out, not_156_out, not_157_out,
       not_158_out, not_159_out, not_160_out, not_161_out, not_162_out, not_163_out, not_164_out,
       not_165_out, not_166_out, not_167_out, not_168_out, not_169_out, not_170_out, not_171_out,
       not_172_out, not_173_out, not_174_out, not_175_out, not_176_out, not_177_out, not_178_out,
       not_179_out, not_180_out, not_181_out, not_182_out, not_183_out, not_184_out, not_185_out,
       not_186_out, not_187_out, not_188_out, not_189_out, not_190_out, not_191_out, not_192_out,
       not_193_out, not_194_out, not_195_out, not_196_out, not_197_out, not_198_out, not_199_out,
       not_200_out, not_201_out, not_202_out, not_203_out, not_204_out, not_205_out, not_206_out,
       not_207_out, not_208_out, not_209_out, not_210_out, not_211_out, not_212_out, not_213_out,
       not_214_out, not_215_out, not_216_out, not_217_out, not_218_out, not_219_out, not_220_out,
       not_221_out, not_222_out, not_223_out, not_224_out, not_225_out, not_226_out, not_227_out,
       not_228_out, not_229_out, not_230_out, not_231_out, not_232_out, not_233_out, not_234_out,
       not_235_out, not_236_out, not_237_out, not_238_out, not_239_out, not_240_out, not_241_out,
       not_242_out, not_243_out, not_244_out, not_245_out, not_246_out, not_247_out, not_248_out,
       not_249_out, not_250_out, not_251_out, not_252_out, not_253_out, not_254_out, not_255_out,
       not_256_out, not_257_out, not_258_out, not_259_out, not_260_out, not_261_out, not_262_out,
       not_263_out, not_264_out, not_265_out, not_266_out, not_267_out, not_268_out, not_269_out,
       not_270_out, or_5_out, or_7_out;

  and and_1 (and_1_out, A3, B3);
  and and_2 (and_2_out, A2, B2, B3);
  and and_3 (and_3_out, A2, A3, B2);
  and and_4 (and_4_out, A1, B1, B2, B3);
  and and_5 (and_5_out, A1, A3, B1, B2);
  and and_6 (and_6_out, A1, A2, B1, B3);
  and and_7 (and_7_out, A1, A2, A3, B1);
  and and_8 (and_8_out, A0, B0, B1, B2, B3);
  and and_9 (and_9_out, A0, A3, B0, B1, B2);
  and and_10 (and_10_out, A0, A2, B0, B1, B3);
  and and_11 (and_11_out, A0, A2, A3, B0, B1);
  and and_12 (and_12_out, A0, A1, B0, B2, B3);
  and and_13 (and_13_out, A0, A1, A3, B0, B2);
  and and_14 (and_14_out, A0, A1, A2, B0, B3);
  and and_15 (and_15_out, A0, A1, A2, A3, B0);
  and and_16 (and_16_out, Cin, B0, B1, B2, B3);
  and and_17 (and_17_out, Cin, A3, B0, B1, B2);
  and and_18 (and_18_out, Cin, A2, B0, B1, B3);
  and and_19 (and_19_out, Cin, A2, A3, B0, B1);
  and and_20 (and_20_out, Cin, A1, B0, B2, B3);
  and and_21 (and_21_out, Cin, A1, A3, B0, B2);
  and and_22 (and_22_out, Cin, A1, A2, B0, B3);
  and and_23 (and_23_out, Cin, A1, A2, A3, B0);
  and and_24 (and_24_out, Cin, A0, B1, B2, B3);
  and and_25 (and_25_out, Cin, A0, A3, B1, B2);
  and and_26 (and_26_out, Cin, A0, A2, B1, B3);
  and and_27 (and_27_out, Cin, A0, A2, A3, B1);
  and and_28 (and_28_out, Cin, A0, A1, B2, B3);
  and and_29 (and_29_out, Cin, A0, A1, A3, B2);
  and and_30 (and_30_out, Cin, A0, A1, A2, B3);
  and and_31 (and_31_out, Cin, A0, A1, A2, A3);
  not not_1 (not_1_out, Cin);
  not not_2 (not_2_out, A0);
  not not_3 (not_3_out, Cin);
  not not_4 (not_4_out, B0);
  not not_5 (not_5_out, A0);
  not not_6 (not_6_out, B0);
  not not_7 (not_7_out, Cin);
  not not_8 (not_8_out, A0);
  not not_9 (not_9_out, A1);
  not not_10 (not_10_out, Cin);
  not not_11 (not_11_out, A1);
  not not_12 (not_12_out, B0);
  not not_13 (not_13_out, A0);
  not not_14 (not_14_out, A1);
  not not_15 (not_15_out, B0);
  not not_16 (not_16_out, Cin);
  not not_17 (not_17_out, A0);
  not not_18 (not_18_out, B1);
  not not_19 (not_19_out, Cin);
  not not_20 (not_20_out, B0);
  not not_21 (not_21_out, B1);
  not not_22 (not_22_out, A0);
  not not_23 (not_23_out, B0);
  not not_24 (not_24_out, B1);
  not not_25 (not_25_out, A1);
  not not_26 (not_26_out, B1);
  not not_27 (not_27_out, A1);
  not not_28 (not_28_out, B1);
  not not_29 (not_29_out, A1);
  not not_30 (not_30_out, B1);
  not not_31 (not_31_out, Cin);
  not not_32 (not_32_out, A0);
  not not_33 (not_33_out, A1);
  not not_34 (not_34_out, A2);
  not not_35 (not_35_out, Cin);
  not not_36 (not_36_out, A0);
  not not_37 (not_37_out, A2);
  not not_38 (not_38_out, B1);
  not not_39 (not_39_out, Cin);
  not not_40 (not_40_out, A1);
  not not_41 (not_41_out, A2);
  not not_42 (not_42_out, B0);
  not not_43 (not_43_out, Cin);
  not not_44 (not_44_out, A2);
  not not_45 (not_45_out, B0);
  not not_46 (not_46_out, B1);
  not not_47 (not_47_out, A0);
  not not_48 (not_48_out, A1);
  not not_49 (not_49_out, A2);
  not not_50 (not_50_out, B0);
  not not_51 (not_51_out, A0);
  not not_52 (not_52_out, A2);
  not not_53 (not_53_out, B0);
  not not_54 (not_54_out, B1);
  not not_55 (not_55_out, A1);
  not not_56 (not_56_out, A2);
  not not_57 (not_57_out, B1);
  not not_58 (not_58_out, Cin);
  not not_59 (not_59_out, A0);
  not not_60 (not_60_out, A1);
  not not_61 (not_61_out, B2);
  not not_62 (not_62_out, Cin);
  not not_63 (not_63_out, A0);
  not not_64 (not_64_out, B1);
  not not_65 (not_65_out, B2);
  not not_66 (not_66_out, Cin);
  not not_67 (not_67_out, A1);
  not not_68 (not_68_out, B0);
  not not_69 (not_69_out, B2);
  not not_70 (not_70_out, Cin);
  not not_71 (not_71_out, B0);
  not not_72 (not_72_out, B1);
  not not_73 (not_73_out, B2);
  not not_74 (not_74_out, A0);
  not not_75 (not_75_out, A1);
  not not_76 (not_76_out, B0);
  not not_77 (not_77_out, B2);
  not not_78 (not_78_out, A0);
  not not_79 (not_79_out, B0);
  not not_80 (not_80_out, B1);
  not not_81 (not_81_out, B2);
  not not_82 (not_82_out, A1);
  not not_83 (not_83_out, B1);
  not not_84 (not_84_out, B2);
  not not_85 (not_85_out, A2);
  not not_86 (not_86_out, B2);
  not not_87 (not_87_out, A2);
  not not_88 (not_88_out, B2);
  not not_89 (not_89_out, A2);
  not not_90 (not_90_out, B2);
  not not_91 (not_91_out, A2);
  not not_92 (not_92_out, B2);
  not not_93 (not_93_out, A2);
  not not_94 (not_94_out, B2);
  not not_95 (not_95_out, A2);
  not not_96 (not_96_out, B2);
  not not_97 (not_97_out, A2);
  not not_98 (not_98_out, B2);
  not not_99 (not_99_out, Cin);
  not not_100 (not_100_out, A0);
  not not_101 (not_101_out, A1);
  not not_102 (not_102_out, A2);
  not not_103 (not_103_out, A3);
  not not_104 (not_104_out, Cin);
  not not_105 (not_105_out, A0);
  not not_106 (not_106_out, A1);
  not not_107 (not_107_out, A3);
  not not_108 (not_108_out, B2);
  not not_109 (not_109_out, Cin);
  not not_110 (not_110_out, A0);
  not not_111 (not_111_out, A2);
  not not_112 (not_112_out, A3);
  not not_113 (not_113_out, B1);
  not not_114 (not_114_out, Cin);
  not not_115 (not_115_out, A0);
  not not_116 (not_116_out, A3);
  not not_117 (not_117_out, B1);
  not not_118 (not_118_out, B2);
  not not_119 (not_119_out, Cin);
  not not_120 (not_120_out, A1);
  not not_121 (not_121_out, A2);
  not not_122 (not_122_out, A3);
  not not_123 (not_123_out, B0);
  not not_124 (not_124_out, Cin);
  not not_125 (not_125_out, A1);
  not not_126 (not_126_out, A3);
  not not_127 (not_127_out, B0);
  not not_128 (not_128_out, B2);
  not not_129 (not_129_out, Cin);
  not not_130 (not_130_out, A2);
  not not_131 (not_131_out, A3);
  not not_132 (not_132_out, B0);
  not not_133 (not_133_out, B1);
  not not_134 (not_134_out, Cin);
  not not_135 (not_135_out, A3);
  not not_136 (not_136_out, B0);
  not not_137 (not_137_out, B1);
  not not_138 (not_138_out, B2);
  not not_139 (not_139_out, A0);
  not not_140 (not_140_out, A1);
  not not_141 (not_141_out, A2);
  not not_142 (not_142_out, A3);
  not not_143 (not_143_out, B0);
  not not_144 (not_144_out, A0);
  not not_145 (not_145_out, A1);
  not not_146 (not_146_out, A3);
  not not_147 (not_147_out, B0);
  not not_148 (not_148_out, B2);
  not not_149 (not_149_out, A0);
  not not_150 (not_150_out, A2);
  not not_151 (not_151_out, A3);
  not not_152 (not_152_out, B0);
  not not_153 (not_153_out, B1);
  not not_154 (not_154_out, A0);
  not not_155 (not_155_out, A3);
  not not_156 (not_156_out, B0);
  not not_157 (not_157_out, B1);
  not not_158 (not_158_out, B2);
  not not_159 (not_159_out, A1);
  not not_160 (not_160_out, A2);
  not not_161 (not_161_out, A3);
  not not_162 (not_162_out, B1);
  not not_163 (not_163_out, A1);
  not not_164 (not_164_out, A3);
  not not_165 (not_165_out, B1);
  not not_166 (not_166_out, B2);
  not not_167 (not_167_out, A2);
  not not_168 (not_168_out, A3);
  not not_169 (not_169_out, B2);
  not not_170 (not_170_out, Cin);
  not not_171 (not_171_out, A0);
  not not_172 (not_172_out, A1);
  not not_173 (not_173_out, A2);
  not not_174 (not_174_out, B3);
  not not_175 (not_175_out, Cin);
  not not_176 (not_176_out, A0);
  not not_177 (not_177_out, A1);
  not not_178 (not_178_out, B2);
  not not_179 (not_179_out, B3);
  not not_180 (not_180_out, Cin);
  not not_181 (not_181_out, A0);
  not not_182 (not_182_out, A2);
  not not_183 (not_183_out, B1);
  not not_184 (not_184_out, B3);
  not not_185 (not_185_out, Cin);
  not not_186 (not_186_out, A0);
  not not_187 (not_187_out, B1);
  not not_188 (not_188_out, B2);
  not not_189 (not_189_out, B3);
  not not_190 (not_190_out, Cin);
  not not_191 (not_191_out, A1);
  not not_192 (not_192_out, A2);
  not not_193 (not_193_out, B0);
  not not_194 (not_194_out, B3);
  not not_195 (not_195_out, Cin);
  not not_196 (not_196_out, A1);
  not not_197 (not_197_out, B0);
  not not_198 (not_198_out, B2);
  not not_199 (not_199_out, B3);
  not not_200 (not_200_out, Cin);
  not not_201 (not_201_out, A2);
  not not_202 (not_202_out, B0);
  not not_203 (not_203_out, B1);
  not not_204 (not_204_out, B3);
  not not_205 (not_205_out, Cin);
  not not_206 (not_206_out, B0);
  not not_207 (not_207_out, B1);
  not not_208 (not_208_out, B2);
  not not_209 (not_209_out, B3);
  not not_210 (not_210_out, A0);
  not not_211 (not_211_out, A1);
  not not_212 (not_212_out, A2);
  not not_213 (not_213_out, B0);
  not not_214 (not_214_out, B3);
  not not_215 (not_215_out, A0);
  not not_216 (not_216_out, A1);
  not not_217 (not_217_out, B0);
  not not_218 (not_218_out, B2);
  not not_219 (not_219_out, B3);
  not not_220 (not_220_out, A0);
  not not_221 (not_221_out, A2);
  not not_222 (not_222_out, B0);
  not not_223 (not_223_out, B1);
  not not_224 (not_224_out, B3);
  not not_225 (not_225_out, A0);
  not not_226 (not_226_out, B0);
  not not_227 (not_227_out, B1);
  not not_228 (not_228_out, B2);
  not not_229 (not_229_out, B3);
  not not_230 (not_230_out, A1);
  not not_231 (not_231_out, A2);
  not not_232 (not_232_out, B1);
  not not_233 (not_233_out, B3);
  not not_234 (not_234_out, A1);
  not not_235 (not_235_out, B1);
  not not_236 (not_236_out, B2);
  not not_237 (not_237_out, B3);
  not not_238 (not_238_out, A2);
  not not_239 (not_239_out, B2);
  not not_240 (not_240_out, B3);
  not not_241 (not_241_out, A3);
  not not_242 (not_242_out, B3);
  not not_243 (not_243_out, A3);
  not not_244 (not_244_out, B3);
  not not_245 (not_245_out, A3);
  not not_246 (not_246_out, B3);
  not not_247 (not_247_out, A3);
  not not_248 (not_248_out, B3);
  not not_249 (not_249_out, A3);
  not not_250 (not_250_out, B3);
  not not_251 (not_251_out, A3);
  not not_252 (not_252_out, B3);
  not not_253 (not_253_out, A3);
  not not_254 (not_254_out, B3);
  not not_255 (not_255_out, A3);
  not not_256 (not_256_out, B3);
  not not_257 (not_257_out, A3);
  not not_258 (not_258_out, B3);
  not not_259 (not_259_out, A3);
  not not_260 (not_260_out, B3);
  not not_261 (not_261_out, A3);
  not not_262 (not_262_out, B3);
  not not_263 (not_263_out, A3);
  not not_264 (not_264_out, B3);
  not not_265 (not_265_out, A3);
  not not_266 (not_266_out, B3);
  not not_267 (not_267_out, A3);
  not not_268 (not_268_out, B3);
  not not_269 (not_269_out, A3);
  not not_270 (not_270_out, B3);
  and and_32 (and_32_out, not_1_out, not_2_out, B0);
  and and_33 (and_33_out, not_3_out, A0, not_4_out);
  and and_34 (and_34_out, Cin, not_5_out, not_6_out);
  and and_35 (and_35_out, Cin, A0, B0);
  and and_36 (and_36_out, not_7_out, not_8_out, not_9_out, B1);
  and and_37 (and_37_out, not_10_out, not_11_out, not_12_out, B1);
  and and_38 (and_38_out, not_13_out, not_14_out, not_15_out, B1);
  and and_39 (and_39_out, not_16_out, not_17_out, A1, not_18_out);
  and and_40 (and_40_out, not_19_out, A1, not_20_out, not_21_out);
  and and_41 (and_41_out, not_22_out, A1, not_23_out, not_24_out);
  and and_42 (and_42_out, A0, not_25_out, B0, not_26_out);
  and and_43 (and_43_out, A0, A1, B0, B1);
  and and_44 (and_44_out, Cin, not_27_out, B0, not_28_out);
  and and_45 (and_45_out, Cin, A1, B0, B1);
  and and_46 (and_46_out, Cin, A0, not_29_out, not_30_out);
  and and_47 (and_47_out, Cin, A0, A1, B1);
  and and_48 (and_48_out, not_31_out, not_32_out, not_33_out, not_34_out, B2);
  and and_49 (and_49_out, not_35_out, not_36_out, not_37_out, not_38_out, B2);
  and and_50 (and_50_out, not_39_out, not_40_out, not_41_out, not_42_out, B2);
  and and_51 (and_51_out, not_43_out, not_44_out, not_45_out, not_46_out, B2);
  and and_52 (and_52_out, not_47_out, not_48_out, not_49_out, not_50_out, B2);
  and and_53 (and_53_out, not_51_out, not_52_out, not_53_out, not_54_out, B2);
  and and_54 (and_54_out, not_55_out, not_56_out, not_57_out, B2);
  and and_55 (and_55_out, not_58_out, not_59_out, not_60_out, A2, not_61_out);
  and and_56 (and_56_out, not_62_out, not_63_out, A2, not_64_out, not_65_out);
  and and_57 (and_57_out, not_66_out, not_67_out, A2, not_68_out, not_69_out);
  and and_58 (and_58_out, not_70_out, A2, not_71_out, not_72_out, not_73_out);
  and and_59 (and_59_out, not_74_out, not_75_out, A2, not_76_out, not_77_out);
  and and_60 (and_60_out, not_78_out, A2, not_79_out, not_80_out, not_81_out);
  and and_61 (and_61_out, not_82_out, A2, not_83_out, not_84_out);
  and and_62 (and_62_out, A1, not_85_out, B1, not_86_out);
  and and_63 (and_63_out, A1, A2, B1, B2);
  and and_64 (and_64_out, A0, not_87_out, B0, B1, not_88_out);
  and and_65 (and_65_out, A0, A2, B0, B1, B2);
  and and_66 (and_66_out, A0, A1, not_89_out, B0, not_90_out);
  and and_67 (and_67_out, A0, A1, A2, B0, B2);
  and and_68 (and_68_out, Cin, not_91_out, B0, B1, not_92_out);
  and and_69 (and_69_out, Cin, A2, B0, B1, B2);
  and and_70 (and_70_out, Cin, A1, not_93_out, B0, not_94_out);
  and and_71 (and_71_out, Cin, A1, A2, B0, B2);
  and and_72 (and_72_out, Cin, A0, not_95_out, B1, not_96_out);
  and and_73 (and_73_out, Cin, A0, A2, B1, B2);
  and and_74 (and_74_out, Cin, A0, A1, not_97_out, not_98_out);
  and and_75 (and_75_out, Cin, A0, A1, A2, B2);
  and and_76 (and_76_out, not_99_out, not_100_out, not_101_out, not_102_out, not_103_out, B3);
  and and_77 (and_77_out, not_104_out, not_105_out, not_106_out, not_107_out, not_108_out, B3);
  and and_78 (and_78_out, not_109_out, not_110_out, not_111_out, not_112_out, not_113_out, B3);
  and and_79 (and_79_out, not_114_out, not_115_out, not_116_out, not_117_out, not_118_out, B3);
  and and_80 (and_80_out, not_119_out, not_120_out, not_121_out, not_122_out, not_123_out, B3);
  and and_81 (and_81_out, not_124_out, not_125_out, not_126_out, not_127_out, not_128_out, B3);
  and and_82 (and_82_out, not_129_out, not_130_out, not_131_out, not_132_out, not_133_out, B3);
  and and_83 (and_83_out, not_134_out, not_135_out, not_136_out, not_137_out, not_138_out, B3);
  and and_84 (and_84_out, not_139_out, not_140_out, not_141_out, not_142_out, not_143_out, B3);
  and and_85 (and_85_out, not_144_out, not_145_out, not_146_out, not_147_out, not_148_out, B3);
  and and_86 (and_86_out, not_149_out, not_150_out, not_151_out, not_152_out, not_153_out, B3);
  and and_87 (and_87_out, not_154_out, not_155_out, not_156_out, not_157_out, not_158_out, B3);
  and and_88 (and_88_out, not_159_out, not_160_out, not_161_out, not_162_out, B3);
  and and_89 (and_89_out, not_163_out, not_164_out, not_165_out, not_166_out, B3);
  and and_90 (and_90_out, not_167_out, not_168_out, not_169_out, B3);
  and and_91 (and_91_out, not_170_out, not_171_out, not_172_out, not_173_out, A3, not_174_out);
  and and_92 (and_92_out, not_175_out, not_176_out, not_177_out, A3, not_178_out, not_179_out);
  and and_93 (and_93_out, not_180_out, not_181_out, not_182_out, A3, not_183_out, not_184_out);
  and and_94 (and_94_out, not_185_out, not_186_out, A3, not_187_out, not_188_out, not_189_out);
  and and_95 (and_95_out, not_190_out, not_191_out, not_192_out, A3, not_193_out, not_194_out);
  and and_96 (and_96_out, not_195_out, not_196_out, A3, not_197_out, not_198_out, not_199_out);
  and and_97 (and_97_out, not_200_out, not_201_out, A3, not_202_out, not_203_out, not_204_out);
  and and_98 (and_98_out, not_205_out, A3, not_206_out, not_207_out, not_208_out, not_209_out);
  and and_99 (and_99_out, not_210_out, not_211_out, not_212_out, A3, not_213_out, not_214_out);
  and and_100 (and_100_out, not_215_out, not_216_out, A3, not_217_out, not_218_out, not_219_out);
  and and_101 (and_101_out, not_220_out, not_221_out, A3, not_222_out, not_223_out, not_224_out);
  and and_102 (and_102_out, not_225_out, A3, not_226_out, not_227_out, not_228_out, not_229_out);
  and and_103 (and_103_out, not_230_out, not_231_out, A3, not_232_out, not_233_out);
  and and_104 (and_104_out, not_234_out, A3, not_235_out, not_236_out, not_237_out);
  and and_105 (and_105_out, not_238_out, A3, not_239_out, not_240_out);
  and and_106 (and_106_out, A2, not_241_out, B2, not_242_out);
  and and_107 (and_107_out, A2, A3, B2, B3);
  and and_108 (and_108_out, A1, not_243_out, B1, B2, not_244_out);
  and and_109 (and_109_out, A1, A3, B1, B2, B3);
  and and_110 (and_110_out, A1, A2, not_245_out, B1, not_246_out);
  and and_111 (and_111_out, A1, A2, A3, B1, B3);
  and and_112 (and_112_out, A0, not_247_out, B0, B1, B2, not_248_out);
  and and_113 (and_113_out, A0, A3, B0, B1, B2, B3);
  and and_114 (and_114_out, A0, A2, not_249_out, B0, B1, not_250_out);
  and and_115 (and_115_out, A0, A2, A3, B0, B1, B3);
  and and_116 (and_116_out, A0, A1, not_251_out, B0, B2, not_252_out);
  and and_117 (and_117_out, A0, A1, A3, B0, B2, B3);
  and and_118 (and_118_out, A0, A1, A2, not_253_out, B0, not_254_out);
  and and_119 (and_119_out, A0, A1, A2, A3, B0, B3);
  and and_120 (and_120_out, Cin, not_255_out, B0, B1, B2, not_256_out);
  and and_121 (and_121_out, Cin, A3, B0, B1, B2, B3);
  and and_122 (and_122_out, Cin, A2, not_257_out, B0, B1, not_258_out);
  and and_123 (and_123_out, Cin, A2, A3, B0, B1, B3);
  and and_124 (and_124_out, Cin, A1, not_259_out, B0, B2, not_260_out);
  and and_125 (and_125_out, Cin, A1, A3, B0, B2, B3);
  and and_126 (and_126_out, Cin, A1, A2, not_261_out, B0, not_262_out);
  and and_127 (and_127_out, Cin, A1, A2, A3, B0, B3);
  and and_128 (and_128_out, Cin, A0, not_263_out, B1, B2, not_264_out);
  and and_129 (and_129_out, Cin, A0, A3, B1, B2, B3);
  and and_130 (and_130_out, Cin, A0, A2, not_265_out, B1, not_266_out);
  and and_131 (and_131_out, Cin, A0, A2, A3, B1, B3);
  and and_132 (and_132_out, Cin, A0, A1, not_267_out, B2, not_268_out);
  and and_133 (and_133_out, Cin, A0, A1, A3, B2, B3);
  and and_134 (and_134_out, Cin, A0, A1, A2, not_269_out, not_270_out);
  and and_135 (and_135_out, Cin, A0, A1, A2, A3, B3);
  or or_1 (R0, and_32_out, and_33_out, and_34_out, and_35_out);
  or or_2 (R1, and_36_out, and_37_out, and_38_out, and_39_out, and_40_out, and_41_out, and_42_out, and_43_out, and_44_out, and_45_out, and_46_out, and_47_out);
  and and_136 (and_136_out, A2, B2);
  or or_3 (Cout, and_1_out, and_2_out, and_3_out, and_4_out, and_5_out, and_6_out, and_7_out, and_8_out, and_9_out, and_10_out, and_11_out, and_12_out, and_13_out, and_14_out, and_15_out, and_16_out, and_17_out, and_18_out, and_19_out, and_20_out, and_21_out, and_22_out, and_23_out, and_24_out, and_25_out, and_26_out, and_27_out, and_28_out, and_29_out, and_30_out, and_31_out);
  or or_4 (R2, and_48_out, and_49_out, and_50_out, and_51_out, and_52_out, and_53_out, and_54_out, and_55_out, and_56_out, and_57_out, and_58_out, and_59_out, and_60_out, and_61_out, and_62_out, and_63_out, and_64_out, and_65_out, and_66_out, and_67_out, and_68_out, and_69_out, and_70_out, and_71_out, and_72_out, and_73_out, and_74_out, and_75_out);
  or or_5 (or_5_out, and_76_out, and_77_out, and_78_out, and_79_out, and_80_out, and_81_out, and_82_out, and_83_out, and_84_out, and_85_out, and_86_out, and_87_out, and_88_out, and_89_out, and_90_out, and_91_out, and_92_out, and_93_out, and_94_out, and_95_out, and_96_out, and_97_out, and_98_out, and_99_out, and_100_out, and_101_out, and_102_out, and_103_out, and_104_out, and_105_out);
  or or_6 (R3, or_5_out, or_7_out);
  or or_7 (or_7_out, and_106_out, and_107_out, and_108_out, and_109_out, and_110_out, and_111_out, and_112_out, and_113_out, and_114_out, and_115_out, and_116_out, and_117_out, and_118_out, and_119_out, and_120_out, and_121_out, and_122_out, and_123_out, and_124_out, and_125_out, and_126_out, and_127_out, and_128_out, and_129_out, and_130_out, and_131_out, and_132_out, and_133_out, and_134_out, and_135_out);
  xor xor_1 (overflow, and_136_out, Cout);

  // Notes on the sheet:
  //   Cin: pull=down
endmodule

module _4_bit_adder (
  input  Cin,
  input  [3:0] A,
  input  [3:0] B,
  output [3:0] Result,
  output Cout,
  output overflow
);

  _4_bit_adder__raw u_4_bit_adder_raw_1 (
    .Cin(Cin), .A0(A[0]), .A1(A[1]), .A2(A[2]), .A3(A[3]), .B0(B[0]), .B1(B[1]), .B2(B[2]), .B3(B[3]),
    .Cout(Cout), .R0(Result[0]), .R1(Result[1]), .R2(Result[2]), .R3(Result[3]), .overflow(overflow));

  // Notes on the sheet:
  //   Cin: pull=down
endmodule

module _32_bit_adder (
  input  Cin,
  input  [31:0] A,
  input  [31:0] B,
  output [31:0] S,
  output Cout,
  output overflow
);

  wire n4_bit_adder_1_cout, n4_bit_adder_2_cout, n4_bit_adder_3_cout, n4_bit_adder_4_cout,
       n4_bit_adder_5_cout, n4_bit_adder_6_cout, n4_bit_adder_7_cout;

  _4_bit_adder u_4_bit_adder_1 (
    .A(A[3:0]), .B(B[3:0]), .Cin(Cin), .Cout(n4_bit_adder_1_cout), .Result(S[3:0]));  // open: overflow
  _4_bit_adder u_4_bit_adder_2 (
    .A(A[7:4]), .B(B[7:4]), .Cin(n4_bit_adder_1_cout), .Cout(n4_bit_adder_2_cout), .Result(S[7:4]));  // open: overflow
  _4_bit_adder u_4_bit_adder_3 (
    .A(A[11:8]), .B(B[11:8]), .Cin(n4_bit_adder_2_cout), .Cout(n4_bit_adder_3_cout), .Result(S[11:8]));  // open: overflow
  _4_bit_adder u_4_bit_adder_4 (
    .A(A[15:12]), .B(B[15:12]), .Cin(n4_bit_adder_3_cout), .Cout(n4_bit_adder_4_cout), .Result(S[15:12]));  // open: overflow
  _4_bit_adder u_4_bit_adder_5 (
    .A(A[19:16]), .B(B[19:16]), .Cin(n4_bit_adder_4_cout), .Cout(n4_bit_adder_5_cout), .Result(S[19:16]));  // open: overflow
  _4_bit_adder u_4_bit_adder_6 (
    .A(A[23:20]), .B(B[23:20]), .Cin(n4_bit_adder_5_cout), .Cout(n4_bit_adder_6_cout), .Result(S[23:20]));  // open: overflow
  _4_bit_adder u_4_bit_adder_7 (
    .A(A[27:24]), .B(B[27:24]), .Cin(n4_bit_adder_6_cout), .Cout(n4_bit_adder_7_cout), .Result(S[27:24]));  // open: overflow
  _4_bit_adder u_4_bit_adder_8 (
    .A(A[31:28]), .B(B[31:28]), .Cin(n4_bit_adder_7_cout), .Cout(Cout), .overflow(overflow), .Result(S[31:28]));

  // Notes on the sheet:
  //   Cin: pull=down
endmodule

module _32_bit_vector_adder__connector (
  input  Cout,
  input  overflow,
  input  Connect,
  input  Cin,
  output Cout2,
  output overflow_2,
  output Cin2
);

  wire and_1_out, and_2_out, not_1_out;

  not not_1 (not_1_out, Connect);
  and and_1 (and_1_out, not_1_out, Cin);
  and and_2 (and_2_out, Cout, Connect);
  or or_1 (Cin2, and_1_out, and_2_out);
  and and_3 (overflow_2, overflow, not_1_out);

  assign Cout2 = Cout;
endmodule

module _32_bit_vector_adder__raw (
  input  in_1,
  input  [3:0] in_2,
  input  [3:0] in_3,
  input  in_4,
  input  in_5,
  input  [3:0] in_6,
  input  [3:0] in_7,
  input  in_8,
  input  in_9,
  input  [3:0] in_10,
  input  [3:0] in_11,
  input  in_12,
  input  in_13,
  input  [3:0] in_14,
  input  [3:0] in_15,
  input  in_16,
  input  in_17,
  input  [3:0] in_18,
  input  [3:0] in_19,
  input  in_20,
  input  in_21,
  input  [3:0] in_22,
  input  [3:0] in_23,
  input  in_24,
  input  in_25,
  input  [3:0] in_26,
  input  [3:0] in_27,
  input  in_28,
  input  in_29,
  input  [3:0] in_30,
  input  [3:0] in_31,
  output [3:0] out_32,
  output out_33,
  output out_34,
  output [3:0] out_35,
  output out_36,
  output out_37,
  output [3:0] out_38,
  output out_39,
  output out_40,
  output [3:0] out_41,
  output out_42,
  output out_43,
  output [3:0] out_44,
  output out_45,
  output out_46,
  output [3:0] out_47,
  output out_48,
  output out_49,
  output [3:0] out_50,
  output out_51,
  output out_52,
  output [3:0] out_53,
  output out_54,
  output out_55
);

  wire n4_bit_adder_1_cout, n4_bit_adder_1_overflow, n4_bit_adder_2_cout, n4_bit_adder_2_overflow,
       n4_bit_adder_3_cout, n4_bit_adder_3_overflow, n4_bit_adder_4_cout, n4_bit_adder_4_overflow,
       n4_bit_adder_5_cout, n4_bit_adder_5_overflow, n4_bit_adder_6_cout, n4_bit_adder_6_overflow,
       n4_bit_adder_7_cout, n4_bit_adder_7_overflow, n32_bit_vector_adder_connector_1_cin2,
       n32_bit_vector_adder_connector_2_cin2, n32_bit_vector_adder_connector_3_cin2,
       n32_bit_vector_adder_connector_4_cin2, n32_bit_vector_adder_connector_5_cin2,
       n32_bit_vector_adder_connector_6_cin2, n32_bit_vector_adder_connector_7_cin2;

  _4_bit_adder u_4_bit_adder_1 (
    .A(in_2), .B(in_3), .Cin(in_1), .Cout(n4_bit_adder_1_cout), .overflow(n4_bit_adder_1_overflow),
    .Result(out_32));
  _32_bit_vector_adder__connector u_32_bit_vector_adder_connector_1 (
    .Connect(in_4), .Cin(in_5), .Cout(n4_bit_adder_1_cout), .overflow(n4_bit_adder_1_overflow),
    .Cin2(n32_bit_vector_adder_connector_1_cin2), .Cout2(out_33), .overflow_2(out_34));
  _4_bit_adder u_4_bit_adder_2 (
    .A(in_6), .B(in_7), .Cin(n32_bit_vector_adder_connector_1_cin2), .Cout(n4_bit_adder_2_cout),
    .overflow(n4_bit_adder_2_overflow), .Result(out_35));
  _32_bit_vector_adder__connector u_32_bit_vector_adder_connector_2 (
    .Connect(in_8), .Cin(in_9), .Cout(n4_bit_adder_2_cout), .overflow(n4_bit_adder_2_overflow),
    .Cin2(n32_bit_vector_adder_connector_2_cin2), .Cout2(out_36), .overflow_2(out_37));
  _4_bit_adder u_4_bit_adder_3 (
    .A(in_10), .B(in_11), .Cin(n32_bit_vector_adder_connector_2_cin2), .Cout(n4_bit_adder_3_cout),
    .overflow(n4_bit_adder_3_overflow), .Result(out_38));
  _32_bit_vector_adder__connector u_32_bit_vector_adder_connector_3 (
    .Connect(in_12), .Cin(in_13), .Cout(n4_bit_adder_3_cout), .overflow(n4_bit_adder_3_overflow),
    .Cin2(n32_bit_vector_adder_connector_3_cin2), .Cout2(out_39), .overflow_2(out_40));
  _4_bit_adder u_4_bit_adder_4 (
    .A(in_14), .B(in_15), .Cin(n32_bit_vector_adder_connector_3_cin2), .Cout(n4_bit_adder_4_cout),
    .overflow(n4_bit_adder_4_overflow), .Result(out_41));
  _32_bit_vector_adder__connector u_32_bit_vector_adder_connector_4 (
    .Connect(in_16), .Cin(in_17), .Cout(n4_bit_adder_4_cout), .overflow(n4_bit_adder_4_overflow),
    .Cin2(n32_bit_vector_adder_connector_4_cin2), .Cout2(out_42), .overflow_2(out_43));
  _4_bit_adder u_4_bit_adder_5 (
    .A(in_18), .B(in_19), .Cin(n32_bit_vector_adder_connector_4_cin2), .Cout(n4_bit_adder_5_cout),
    .overflow(n4_bit_adder_5_overflow), .Result(out_44));
  _32_bit_vector_adder__connector u_32_bit_vector_adder_connector_5 (
    .Connect(in_20), .Cin(in_21), .Cout(n4_bit_adder_5_cout), .overflow(n4_bit_adder_5_overflow),
    .Cin2(n32_bit_vector_adder_connector_5_cin2), .Cout2(out_45), .overflow_2(out_46));
  _4_bit_adder u_4_bit_adder_6 (
    .A(in_22), .B(in_23), .Cin(n32_bit_vector_adder_connector_5_cin2), .Cout(n4_bit_adder_6_cout),
    .overflow(n4_bit_adder_6_overflow), .Result(out_47));
  _32_bit_vector_adder__connector u_32_bit_vector_adder_connector_6 (
    .Connect(in_24), .Cin(in_25), .Cout(n4_bit_adder_6_cout), .overflow(n4_bit_adder_6_overflow),
    .Cin2(n32_bit_vector_adder_connector_6_cin2), .Cout2(out_48), .overflow_2(out_49));
  _4_bit_adder u_4_bit_adder_7 (
    .A(in_26), .B(in_27), .Cin(n32_bit_vector_adder_connector_6_cin2), .Cout(n4_bit_adder_7_cout),
    .overflow(n4_bit_adder_7_overflow), .Result(out_50));
  _32_bit_vector_adder__connector u_32_bit_vector_adder_connector_7 (
    .Connect(in_28), .Cin(in_29), .Cout(n4_bit_adder_7_cout), .overflow(n4_bit_adder_7_overflow),
    .Cin2(n32_bit_vector_adder_connector_7_cin2), .Cout2(out_51), .overflow_2(out_52));
  _4_bit_adder u_4_bit_adder_8 (
    .A(in_30), .B(in_31), .Cin(n32_bit_vector_adder_connector_7_cin2), .Cout(out_54), .overflow(out_55),
    .Result(out_53));
endmodule

module _32_bit_vector_adder (
  input  [7:0] Cin,
  input  [31:0] A,
  input  [31:0] B,
  input  [6:0] Connect,
  output [31:0] S,
  output [7:0] overflow,
  output [7:0] Cout
);

  _32_bit_vector_adder__raw u_32_bit_vector_adder_raw_1 (
    .in_2(A[3:0]), .in_3(B[3:0]), .in_4(Connect[0]), .in_6(A[7:4]), .in_7(B[7:4]), .in_8(Connect[1]),
    .in_10(A[11:8]), .in_11(B[11:8]), .in_12(Connect[2]), .in_14(A[15:12]), .in_15(B[15:12]),
    .in_16(Connect[3]), .in_18(A[19:16]), .in_19(B[19:16]), .in_20(Connect[4]), .in_22(A[23:20]),
    .in_23(B[23:20]), .in_24(Connect[5]), .in_26(A[27:24]), .in_27(B[27:24]), .in_28(Connect[6]),
    .in_30(A[31:28]), .in_31(B[31:28]), .out_32(S[3:0]), .out_35(S[7:4]), .out_38(S[11:8]),
    .out_41(S[15:12]), .out_44(S[19:16]), .out_47(S[23:20]), .out_50(S[27:24]), .out_53(S[31:28]),
    .in_5(Cin[1]), .in_9(Cin[2]), .in_13(Cin[3]), .in_17(Cin[4]), .in_21(Cin[5]), .in_25(Cin[6]),
    .in_29(Cin[7]), .in_1(Cin[0]), .out_33(Cout[0]), .out_36(Cout[1]), .out_39(Cout[2]), .out_42(Cout[3]),
    .out_45(Cout[4]), .out_48(Cout[5]), .out_51(Cout[6]), .out_54(Cout[7]), .out_34(overflow[0]),
    .out_37(overflow[1]), .out_40(overflow[2]), .out_43(overflow[3]), .out_46(overflow[4]),
    .out_49(overflow[5]), .out_52(overflow[6]), .out_55(overflow[7]));

  // Notes on the sheet:
  //   Connect: pull=up
  //   Cin: pull=down
endmodule

module _32_bit_vector_adder__wrap (
  input  Cin,
  input  [31:0] A,
  input  [31:0] B,
  output [31:0] S,
  output Cout,
  output overflow
);

  wire [6:0] n32_bit_vector_adder_1_cout, n32_bit_vector_adder_1_overflow;
  wire [7:0] bit_extender_1_out;

  assign bit_extender_1_out = {{7{1'b0}}, Cin};  // Bit_Extender bit_extender_1
  _32_bit_vector_adder u_32_bit_vector_adder_1 (
    .A(A), .B(B), .Connect({7{1'b1}}), .Cin(bit_extender_1_out), .Cout({Cout, n32_bit_vector_adder_1_cout}),
    .S(S), .overflow({overflow, n32_bit_vector_adder_1_overflow}));

  // Notes on the sheet:
  //   Cin: pull=down
endmodule

module ALU__control (
  input  [3:0] funct,
  output [1:0] result_select,
  output sub,
  output [1:0] logic_control,
  output [2:0] shift_control
);

  wire alu_control_and_1_add, alu_control_and_1_and, alu_control_and_1_nor, alu_control_and_1_or,
       alu_control_and_1_sll, alu_control_and_1_sra, alu_control_and_1_srl, alu_control_and_1_sub,
       alu_control_and_1_xor;

  ALU__control__and alu_control_and_1 (
    .funct(funct), .\and (alu_control_and_1_and), .\or (alu_control_and_1_or), .\nor (alu_control_and_1_nor),
    .\xor (alu_control_and_1_xor), .add(alu_control_and_1_add), .sub(alu_control_and_1_sub),
    .sll(alu_control_and_1_sll), .srl(alu_control_and_1_srl), .sra(alu_control_and_1_sra));
  ALU__control__or alu_control_or_1 (
    .\and (alu_control_and_1_and), .\or (alu_control_and_1_or), .\nor (alu_control_and_1_nor),
    .\xor (alu_control_and_1_xor), .add(alu_control_and_1_add), .sub(alu_control_and_1_sub),
    .sll(alu_control_and_1_sll), .srl(alu_control_and_1_srl), .sra(alu_control_and_1_sra),
    .result_select(result_select), .sub_2(sub), .logic_control(logic_control), .shift_control(shift_control));
endmodule

module _1bit_comparer (
  input  A,
  input  B,
  input  \signed ,
  output gt,
  output eq,
  output lt
);

  wire and_1_out, and_2_out, and_3_out, and_4_out, not_1_out, not_2_out, not_3_out, not_4_out, not_5_out,
       not_6_out;

  not not_1 (not_1_out, \signed );
  not not_2 (not_2_out, B);
  not not_3 (not_3_out, A);
  not not_4 (not_4_out, \signed );
  not not_5 (not_5_out, A);
  not not_6 (not_6_out, B);
  and and_1 (and_1_out, not_1_out, A, not_2_out);
  and and_2 (and_2_out, \signed , not_3_out, B);
  xnor xnor_1 (eq, A, B);
  and and_3 (and_3_out, not_4_out, not_5_out, B);
  and and_4 (and_4_out, \signed , A, not_6_out);
  or or_1 (gt, and_1_out, and_2_out);
  or or_2 (lt, and_3_out, and_4_out);

  // Notes on the sheet:
  //   signed: pull=down
endmodule

module comparer_merge (
  input  low_gt,
  input  low_eq,
  input  low_lt,
  input  high_gt,
  input  high_eq,
  input  high_lt,
  output gt,
  output eq,
  output lt
);

  wire and_1_out, and_2_out;

  and and_1 (and_1_out, low_gt, high_eq);
  and and_2 (and_2_out, low_lt, high_eq);
  or or_1 (gt, high_gt, and_1_out);
  and and_3 (eq, low_eq, high_eq);
  or or_2 (lt, and_2_out, high_lt);
endmodule

module _2bit_comparer (
  input  [1:0] A,
  input  [1:0] B,
  output gt,
  output eq,
  output lt
);

  wire n1bit_comparer_1_eq, n1bit_comparer_1_gt, n1bit_comparer_1_lt, n1bit_comparer_2_eq,
       n1bit_comparer_2_gt, n1bit_comparer_2_lt;

  _1bit_comparer u_1bit_comparer_1 (
    .A(A[0]), .B(B[0]), .gt(n1bit_comparer_1_gt), .eq(n1bit_comparer_1_eq), .lt(n1bit_comparer_1_lt));  // open: signed
  comparer_merge comparer_merge_1 (
    .low_gt(n1bit_comparer_1_gt), .low_eq(n1bit_comparer_1_eq), .low_lt(n1bit_comparer_1_lt),
    .high_gt(n1bit_comparer_2_gt), .high_eq(n1bit_comparer_2_eq), .high_lt(n1bit_comparer_2_lt), .gt(gt),
    .eq(eq), .lt(lt));
  _1bit_comparer u_1bit_comparer_2 (
    .A(A[1]), .B(B[1]), .gt(n1bit_comparer_2_gt), .eq(n1bit_comparer_2_eq), .lt(n1bit_comparer_2_lt));  // open: signed
endmodule

module _4bit_comparer (
  input  [3:0] A,
  input  [3:0] B,
  output gt,
  output eq,
  output lt
);

  wire n2bit_comparer_1_eq, n2bit_comparer_1_gt, n2bit_comparer_1_lt, n2bit_comparer_2_eq,
       n2bit_comparer_2_gt, n2bit_comparer_2_lt;

  _2bit_comparer u_2bit_comparer_1 (
    .A(A[1:0]), .B(B[1:0]), .gt(n2bit_comparer_1_gt), .eq(n2bit_comparer_1_eq), .lt(n2bit_comparer_1_lt));
  comparer_merge comparer_merge_1 (
    .low_gt(n2bit_comparer_1_gt), .low_eq(n2bit_comparer_1_eq), .low_lt(n2bit_comparer_1_lt),
    .high_gt(n2bit_comparer_2_gt), .high_eq(n2bit_comparer_2_eq), .high_lt(n2bit_comparer_2_lt), .gt(gt),
    .eq(eq), .lt(lt));
  _2bit_comparer u_2bit_comparer_2 (
    .A(A[3:2]), .B(B[3:2]), .gt(n2bit_comparer_2_gt), .eq(n2bit_comparer_2_eq), .lt(n2bit_comparer_2_lt));
endmodule

module _8bit_comparer (
  input  [7:0] A,
  input  [7:0] B,
  output gt,
  output eq,
  output lt
);

  wire n4bit_comparer_1_eq, n4bit_comparer_1_gt, n4bit_comparer_1_lt, n4bit_comparer_2_eq,
       n4bit_comparer_2_gt, n4bit_comparer_2_lt;

  _4bit_comparer u_4bit_comparer_1 (
    .A(A[3:0]), .B(B[3:0]), .gt(n4bit_comparer_1_gt), .eq(n4bit_comparer_1_eq), .lt(n4bit_comparer_1_lt));
  comparer_merge comparer_merge_1 (
    .low_gt(n4bit_comparer_1_gt), .low_eq(n4bit_comparer_1_eq), .low_lt(n4bit_comparer_1_lt),
    .high_gt(n4bit_comparer_2_gt), .high_eq(n4bit_comparer_2_eq), .high_lt(n4bit_comparer_2_lt), .gt(gt),
    .eq(eq), .lt(lt));
  _4bit_comparer u_4bit_comparer_2 (
    .A(A[7:4]), .B(B[7:4]), .gt(n4bit_comparer_2_gt), .eq(n4bit_comparer_2_eq), .lt(n4bit_comparer_2_lt));
endmodule

module _16bit_comparer (
  input  [15:0] A,
  input  [15:0] B,
  output gt,
  output eq,
  output lt
);

  wire n8bit_comparer_1_eq, n8bit_comparer_1_gt, n8bit_comparer_1_lt, n8bit_comparer_2_eq,
       n8bit_comparer_2_gt, n8bit_comparer_2_lt;

  _8bit_comparer u_8bit_comparer_1 (
    .A(A[7:0]), .B(B[7:0]), .gt(n8bit_comparer_1_gt), .eq(n8bit_comparer_1_eq), .lt(n8bit_comparer_1_lt));
  comparer_merge comparer_merge_1 (
    .low_gt(n8bit_comparer_1_gt), .low_eq(n8bit_comparer_1_eq), .low_lt(n8bit_comparer_1_lt),
    .high_gt(n8bit_comparer_2_gt), .high_eq(n8bit_comparer_2_eq), .high_lt(n8bit_comparer_2_lt), .gt(gt),
    .eq(eq), .lt(lt));
  _8bit_comparer u_8bit_comparer_2 (
    .A(A[15:8]), .B(B[15:8]), .gt(n8bit_comparer_2_gt), .eq(n8bit_comparer_2_eq), .lt(n8bit_comparer_2_lt));
endmodule

module _32bit_comparer (
  input  \signed ,
  input  [31:0] A,
  input  [31:0] B,
  output gt,
  output eq,
  output lt
);

  wire comparer_merge_1_eq, comparer_merge_1_gt, comparer_merge_1_lt, comparer_merge_2_eq,
       comparer_merge_2_gt, comparer_merge_2_lt, comparer_merge_3_eq, comparer_merge_3_gt,
       comparer_merge_3_lt, comparer_merge_4_eq, comparer_merge_4_gt, comparer_merge_4_lt,
       n1bit_comparer_1_eq, n1bit_comparer_1_gt, n1bit_comparer_1_lt, n1bit_comparer_2_eq,
       n1bit_comparer_2_gt, n1bit_comparer_2_lt, n2bit_comparer_1_eq, n2bit_comparer_1_gt,
       n2bit_comparer_1_lt, n4bit_comparer_1_eq, n4bit_comparer_1_gt, n4bit_comparer_1_lt,
       n8bit_comparer_1_eq, n8bit_comparer_1_gt, n8bit_comparer_1_lt, n16bit_comparer_1_eq,
       n16bit_comparer_1_gt, n16bit_comparer_1_lt;

  _16bit_comparer u_16bit_comparer_1 (
    .A(A[15:0]), .B(B[15:0]), .gt(n16bit_comparer_1_gt), .eq(n16bit_comparer_1_eq), .lt(n16bit_comparer_1_lt));
  _8bit_comparer u_8bit_comparer_1 (
    .A(A[23:16]), .B(B[23:16]), .gt(n8bit_comparer_1_gt), .eq(n8bit_comparer_1_eq), .lt(n8bit_comparer_1_lt));
  _4bit_comparer u_4bit_comparer_1 (
    .A(A[27:24]), .B(B[27:24]), .gt(n4bit_comparer_1_gt), .eq(n4bit_comparer_1_eq), .lt(n4bit_comparer_1_lt));
  _2bit_comparer u_2bit_comparer_1 (
    .A(A[29:28]), .B(B[29:28]), .gt(n2bit_comparer_1_gt), .eq(n2bit_comparer_1_eq), .lt(n2bit_comparer_1_lt));
  _1bit_comparer u_1bit_comparer_1 (
    .A(A[30]), .B(B[30]), .gt(n1bit_comparer_1_gt), .eq(n1bit_comparer_1_eq), .lt(n1bit_comparer_1_lt));  // open: signed
  _1bit_comparer u_1bit_comparer_2 (
    .A(A[31]), .B(B[31]), .\signed (\signed ), .gt(n1bit_comparer_2_gt), .eq(n1bit_comparer_2_eq),
    .lt(n1bit_comparer_2_lt));
  comparer_merge comparer_merge_1 (
    .low_gt(n16bit_comparer_1_gt), .low_eq(n16bit_comparer_1_eq), .low_lt(n16bit_comparer_1_lt),
    .high_gt(n8bit_comparer_1_gt), .high_eq(n8bit_comparer_1_eq), .high_lt(n8bit_comparer_1_lt),
    .gt(comparer_merge_1_gt), .eq(comparer_merge_1_eq), .lt(comparer_merge_1_lt));
  comparer_merge comparer_merge_2 (
    .low_gt(n4bit_comparer_1_gt), .low_eq(n4bit_comparer_1_eq), .low_lt(n4bit_comparer_1_lt),
    .high_gt(n2bit_comparer_1_gt), .high_eq(n2bit_comparer_1_eq), .high_lt(n2bit_comparer_1_lt),
    .gt(comparer_merge_2_gt), .eq(comparer_merge_2_eq), .lt(comparer_merge_2_lt));
  comparer_merge comparer_merge_3 (
    .low_gt(n1bit_comparer_1_gt), .low_eq(n1bit_comparer_1_eq), .low_lt(n1bit_comparer_1_lt),
    .high_gt(n1bit_comparer_2_gt), .high_eq(n1bit_comparer_2_eq), .high_lt(n1bit_comparer_2_lt),
    .gt(comparer_merge_3_gt), .eq(comparer_merge_3_eq), .lt(comparer_merge_3_lt));
  comparer_merge comparer_merge_4 (
    .low_gt(comparer_merge_1_gt), .low_eq(comparer_merge_1_eq), .low_lt(comparer_merge_1_lt),
    .high_gt(comparer_merge_2_gt), .high_eq(comparer_merge_2_eq), .high_lt(comparer_merge_2_lt),
    .gt(comparer_merge_4_gt), .eq(comparer_merge_4_eq), .lt(comparer_merge_4_lt));
  comparer_merge comparer_merge_5 (
    .low_gt(comparer_merge_4_gt), .low_eq(comparer_merge_4_eq), .low_lt(comparer_merge_4_lt),
    .high_gt(comparer_merge_3_gt), .high_eq(comparer_merge_3_eq), .high_lt(comparer_merge_3_lt), .gt(gt),
    .eq(eq), .lt(lt));
endmodule

module ALU__control__and (
  input  [3:0] funct,
  output \and ,
  output \or ,
  output \nor ,
  output \xor ,
  output add,
  output sub,
  output sll,
  output srl,
  output sra
);

  wire not_1_out, not_2_out, not_3_out, not_4_out;

  not not_1 (not_1_out, funct[0]);
  not not_2 (not_2_out, funct[1]);
  not not_3 (not_3_out, funct[2]);
  not not_4 (not_4_out, funct[3]);
  and and_1 (\and , not_1_out, not_2_out, not_3_out, not_4_out);
  and and_2 (\or , funct[0], not_2_out, not_3_out, not_4_out);
  and and_3 (\nor , not_1_out, funct[1], not_3_out, not_4_out);
  and and_4 (\xor , funct[0], funct[1], not_3_out, not_4_out);
  and and_5 (add, not_1_out, not_2_out, funct[2], not_4_out);
  and and_6 (sub, funct[0], not_2_out, funct[2], not_4_out);
  and and_7 (sll, not_1_out, funct[1], funct[2], not_4_out);
  and and_8 (srl, funct[0], funct[1], funct[2], not_4_out);
  and and_9 (sra, not_1_out, not_2_out, not_3_out, funct[3]);
endmodule

module ALU__control__or (
  input  \and ,
  input  \or ,
  input  \nor ,
  input  \xor ,
  input  add,
  input  sub,
  input  sll,
  input  srl,
  input  sra,
  output [1:0] result_select,
  output sub_2,
  output [1:0] logic_control,
  output [2:0] shift_control
);

  wire \logic ;

  or or_1 (\logic , \and , \or , \nor , \xor );
  or or_2 (result_select[0], add, sub);
  or or_3 (result_select[1], sll, srl, sra);
  or or_4 (logic_control[0], \or , \xor );
  or or_5 (logic_control[1], \xor , \nor );

  assign shift_control = {1'b0, sra, srl};
  assign sub_2 = sub;

  // Other names for the same wires on the sheet: arithmetic = result_select[0]; shifter = result_select[1]
endmodule

module ALU__logic (
  input  [1:0] control,
  input  [31:0] A,
  input  [31:0] B,
  output [31:0] Res
);

  wire [31:0] and_1_out, not_1_out, or_1_out, xor_1_out;

  assign and_1_out = B & A;  // AND_Gate and_1, 32 bits wide
  assign or_1_out = B | A;  // OR_Gate or_1, 32 bits wide
  assign not_1_out = ~or_1_out;  // NOT_Gate not_1, 32 bits wide
  assign xor_1_out = A ^ B;  // XOR_Gate xor_1, 32 bits wide
  Multiplexer #(.select(2), .width(32), .enable("false")) multiplexer_1 (
    .in0(and_1_out), .in1(or_1_out), .in2(not_1_out), .in3(xor_1_out), .out(Res), .sel(control));
endmodule

module ALU__arithmetic (
  input  sub,
  input  [31:0] A,
  input  [31:0] B,
  output [31:0] S,
  output overflow
);

  wire [31:0] multiplexer_1_out, not_1_out;

  assign not_1_out = ~B;  // NOT_Gate not_1, 32 bits wide
  Multiplexer #(.width(32), .enable("false")) multiplexer_1 (
    .in0(B), .in1(not_1_out), .out(multiplexer_1_out), .sel(sub));
  _32_bit_vector_adder__wrap u_32_bit_vector_adder_wrap_1 (
    .A(A), .B(multiplexer_1_out), .Cin(sub), .overflow(overflow), .S(S));  // open: Cout

  // Notes on the sheet:
  //   sub: pull=down
endmodule

module ALU__shifter (
  input  [2:0] control,
  input  [31:0] A,
  input  [4:0] B,
  output [31:0] S
);

  wire [31:0] shifter_1_out, shifter_2_out, shifter_3_out, shifter_4_out, shifter_5_out;

  Shifter #(.width(32)) shifter_1 (.in(A), .\dist (B), .out(shifter_1_out));
  Shifter #(.width(32), .shift("lr")) shifter_2 (.in(A), .\dist (B), .out(shifter_2_out));
  Shifter #(.width(32), .shift("ar")) shifter_3 (.in(A), .\dist (B), .out(shifter_3_out));
  Shifter #(.width(32), .shift("rl")) shifter_4 (.in(A), .\dist (B), .out(shifter_4_out));
  Shifter #(.width(32), .shift("rr")) shifter_5 (.in(A), .\dist (B), .out(shifter_5_out));
  Multiplexer #(.select(3), .width(32), .enable("false")) multiplexer_1 (
    .in0(shifter_1_out), .in1(shifter_2_out), .in2(shifter_3_out), .in3(shifter_4_out), .in4(shifter_5_out),
    .out(S), .sel(control));  // open: in5, in6, in7
endmodule
