// Logisim project CPU.circ as structural Verilog: 3 circuits, main circuit main
module main (
  input  Reset
);

  wire _1, alu_1_eq, alu_1_gt, alu_1_lt, ALU_overflow, ALU_sign_compare, ALU_zero, clock, dm_read, dm_write,
       eq, EXT_signed, ge, grf_write_enable, gt, le, lt, ne, SRF_read_select;
  wire [1:0] addr_select, ALU_A_select, ALU_B_select, ALU_W_select, grf_write_addr_select, jump_ctrl,
       jump_temp;
  wire [1:1] multiplexer_4_out;
  wire [2:0] compare_select, grf_write_data_select;
  wire [3:0] ALU_ctrl, SRF_ctrl;
  wire [4:0] ALU_W, grf_read_addr0, grf_read_addr1, grf_write_addr, rd, shamt;
  wire [5:0] funct, opcode;
  wire [15:0] EXT_in;
  wire [25:0] address;
  wire [31:0] addr, addr_combine_1_combined, ALU_A, ALU_B, ALU_S, bit_extender_1_out, dm_read_data,
       dm_write_data, EXT_out, grf_read0, grf_write_data, Instruction, PC_4, sll2, srf_1_hi, srf_1_lo,
       SRF_read;

  Clock clock_1 (.out(clock));
  IFU ifu_1 (
    .\input (addr), .Instruction(Instruction), .PC_4(PC_4), .PC_select(jump_ctrl), .Clock(clock),
    .Reset(Reset));
  Multiplexer #(.select(2), .width(32), .enable("false")) multiplexer_1 (
    .in0(grf_read0), .in1(EXT_out), .in2(dm_write_data), .out(ALU_A), .sel(ALU_A_select));  // open: in3
  InstructionSplitter instructionsplitter_1 (
    .Instruction(Instruction), .address(address), .offset(EXT_in), .funct(funct), .shamt(shamt), .rd(rd),
    .rt(grf_read_addr1), .rs(grf_read_addr0), .opcode(opcode));
  EXT ext_1 (.Src(EXT_in), .out_3(EXT_out), .Signed(EXT_signed));
  SRF srf_1 (
    .A(grf_read0), .B(dm_write_data), .LO(srf_1_lo), .HI(srf_1_hi), .control(SRF_ctrl), .clock(clock),
    .reset(Reset));
  Shifter #(.width(32)) shifter_1 (.in(EXT_out), .\dist (5'b00010), .out(sll2));
  Multiplexer #(.select(2), .width(5), .enable("false")) multiplexer_2 (
    .in0(5'b10000), .in1(shamt), .in2(grf_read0[4:0]), .out(ALU_W), .sel(ALU_W_select));  // open: in3
  Multiplexer #(.width(32), .enable("false")) multiplexer_3 (
    .in0(srf_1_lo), .in1(srf_1_hi), .out(SRF_read), .sel(SRF_read_select));
  GRF grf_1 (
    .Input(grf_write_data), .read_addr0(grf_read_addr0), .read_addr1(grf_read_addr1),
    .write_enable(grf_write_enable), .write_addr(grf_write_addr), .out_8(grf_read0), .out_9(dm_write_data),
    .Clock(clock), .Reset(Reset));
  ALU alu_1 (
    .A(ALU_A), .B(ALU_B), .shift(ALU_W), .S(ALU_S), .gt(alu_1_gt), .eq(alu_1_eq), .lt(alu_1_lt),
    .funct(ALU_ctrl), .signed_compare(ALU_sign_compare), .zero(ALU_zero), .overflow(ALU_overflow));
  comparer_extender comparer_extender_1 (
    .WHATEVER(_1), .lt(alu_1_lt), .eq(alu_1_eq), .gt(alu_1_gt), .lt_2(lt), .le(le), .eq_2(eq), .ge(ge),
    .gt_2(gt), .ne(ne));
  addr_combine addr_combine_1 (.address(address), .PC_4(PC_4), .combined(addr_combine_1_combined));
  Multiplexer #(.select(3), .enable("false")) multiplexer_4 (
    .in0(lt), .in1(le), .in2(eq), .in3(ge), .in4(gt), .in5(ne), .in6(_1), .out(multiplexer_4_out[1]),
    .sel(compare_select));  // open: in7
  Multiplexer #(.select(2), .width(32), .enable("false")) multiplexer_5 (
    .in0(sll2), .in1(addr_combine_1_combined), .in2(grf_read0), .out(addr), .sel(addr_select));  // open: in3
  DM dm_1 (
    .Addr(ALU_S), .Data(dm_write_data), .Output(dm_read_data), .S(dm_write), .Clock(clock), .L(dm_read),
    .C(Reset));
  assign jump_ctrl = {2{multiplexer_4_out[1]}} & jump_temp;  // AND_Gate and_1, 2 bits wide
  Multiplexer #(.select(2), .width(5), .enable("false")) multiplexer_6 (
    .in0(rd), .in1(grf_read_addr1), .in2({5{1'b1}}), .out(grf_write_addr), .sel(grf_write_addr_select));  // open: in3
  Multiplexer #(.select(2), .width(32), .enable("false")) multiplexer_7 (
    .in0(dm_write_data), .in1(EXT_out), .in2({32{1'b0}}), .out(ALU_B), .sel(ALU_B_select));  // open: in3
  assign bit_extender_1_out = {{31{1'b0}}, lt};  // Bit_Extender bit_extender_1
  Controller controller_1 (
    .Op(opcode), .Func(funct), .extra(grf_read_addr1), .SRF_ctrl(SRF_ctrl), .ALU_B_select(ALU_B_select),
    .ALU_A_select(ALU_A_select), .ALU_W_select(ALU_W_select), .addr_select(addr_select),
    .SRF_read_select(SRF_read_select), .GRF_write_data_select(grf_write_data_select),
    .GRF_write_addr_select(grf_write_addr_select), .grf_write_enable(grf_write_enable),
    .EXT_signed(EXT_signed), .ALU_ctrl(ALU_ctrl), .ALU_sign_compare(ALU_sign_compare), .DM_write(dm_write),
    .DM_read(dm_read), .jump_control(jump_temp), .cmp_select(compare_select));
  Multiplexer #(.select(3), .width(32), .enable("false")) multiplexer_8 (
    .in0(ALU_S), .in1(PC_4), .in2(dm_read_data), .in3(SRF_read), .in4(bit_extender_1_out),
    .out(grf_write_data), .sel(grf_write_data_select));  // open: in5, in6, in7

  // Other names for the same wires on the sheet: dm_read_addr[31:0] = ALU_S; SRF_A[31:0] = grf_read0;
  //   grf_read1[31:0] = dm_write_data; SRF_B[31:0] = dm_write_data; offset[15:0] = EXT_in; rs[4:0] = grf_read_addr0;
  //   rt[4:0] = grf_read_addr1
endmodule

module comparer_extender (
  input  lt,
  input  eq,
  input  gt,
  output ne,
  output WHATEVER,
  output lt_2,
  output le,
  output eq_2,
  output ge,
  output gt_2
);

  not not_1 (ne, eq);
  or or_1 (ge, eq, gt);
  or or_2 (le, lt, eq);
  or or_3 (WHATEVER, lt, eq, gt);

  assign eq_2 = eq;
  assign gt_2 = gt;
  assign lt_2 = lt;
endmodule

module addr_combine (
  input  [25:0] address,
  input  [31:0] PC_4,
  output [31:0] combined
);


  assign combined = {PC_4[31:28], address, 2'b00};
endmodule
