// Logisim project Controller.circ as structural Verilog: 7 circuits, main circuit Controller
module Controller (
  input  [5:0] Op,
  input  [5:0] Func,
  input  [4:0] extra,
  output [3:0] SRF_ctrl,
  output [1:0] ALU_B_select,
  output [1:0] ALU_A_select,
  output [1:0] ALU_W_select,
  output [1:0] addr_select,
  output SRF_read_select,
  output [2:0] GRF_write_data_select,
  output [1:0] GRF_write_addr_select,
  output grf_write_enable,
  output EXT_signed,
  output [3:0] ALU_ctrl,
  output ALU_sign_compare,
  output DM_write,
  output DM_read,
  output [1:0] jump_control,
  output [2:0] cmp_select
);

  wire andlogic_1_add, andlogic_1_addi, andlogic_1_addiu, andlogic_1_addu, andlogic_1_and, andlogic_1_andi,
       andlogic_1_beq, andlogic_1_bgez, andlogic_1_bgezal, andlogic_1_bgtz, andlogic_1_blez, andlogic_1_bltz,
       andlogic_1_bltzal, andlogic_1_bne, andlogic_1_div, andlogic_1_divu, andlogic_1_j, andlogic_1_jal,
       andlogic_1_jalr, andlogic_1_jr, andlogic_1_lui, andlogic_1_lw, andlogic_1_mfhi, andlogic_1_mflo,
       andlogic_1_mthi, andlogic_1_mtlo, andlogic_1_mult, andlogic_1_multu, andlogic_1_nor, andlogic_1_or,
       andlogic_1_ori, andlogic_1_sll, andlogic_1_sllv, andlogic_1_slt, andlogic_1_slti, andlogic_1_sltiu,
       andlogic_1_sltu, andlogic_1_sra, andlogic_1_srav, andlogic_1_srl, andlogic_1_srlv, andlogic_1_sub,
       andlogic_1_subu, andlogic_1_sw, andlogic_1_xor, andlogic_1_xori, orlogic_1_beq_2, orlogic_1_bgez_2,
       orlogic_1_bgezal_2, orlogic_1_bgtz_2, orlogic_1_blez_2, orlogic_1_bltz_2, orlogic_1_bltzal_2,
       orlogic_1_bne_2, orlogic_1_j_2, orlogic_1_jal_2, orlogic_1_jalr_2, orlogic_1_jr_2;

  AndLogic andlogic_1 (
    .OperationCode(Op), .Function(Func), .extra(extra), .addi(andlogic_1_addi), .addiu(andlogic_1_addiu),
    .andi(andlogic_1_andi), .beq(andlogic_1_beq), .bgtz(andlogic_1_bgtz), .blez(andlogic_1_blez),
    .bne(andlogic_1_bne), .j(andlogic_1_j), .jal(andlogic_1_jal), .lui(andlogic_1_lui), .lw(andlogic_1_lw),
    .ori(andlogic_1_ori), .slti(andlogic_1_slti), .sltiu(andlogic_1_sltiu), .sw(andlogic_1_sw),
    .xori(andlogic_1_xori), .add(andlogic_1_add), .addu(andlogic_1_addu), .\and (andlogic_1_and),
    .div(andlogic_1_div), .divu(andlogic_1_divu), .jalr(andlogic_1_jalr), .jr(andlogic_1_jr),
    .mfhi(andlogic_1_mfhi), .mflo(andlogic_1_mflo), .mthi(andlogic_1_mthi), .mtlo(andlogic_1_mtlo),
    .mult(andlogic_1_mult), .multu(andlogic_1_multu), .\nor (andlogic_1_nor), .\or (andlogic_1_or),
    .sll(andlogic_1_sll), .sllv(andlogic_1_sllv), .slt(andlogic_1_slt), .sltu(andlogic_1_sltu),
    .sra(andlogic_1_sra), .srav(andlogic_1_srav), .srl(andlogic_1_srl), .srlv(andlogic_1_srlv),
    .sub(andlogic_1_sub), .subu(andlogic_1_subu), .\xor (andlogic_1_xor), .bgez(andlogic_1_bgez),
    .bgezal(andlogic_1_bgezal), .bltz(andlogic_1_bltz), .bltzal(andlogic_1_bltzal));
  OrLogic orlogic_1 (
    .addi(andlogic_1_addi), .addiu(andlogic_1_addiu), .andi(andlogic_1_andi), .beq(andlogic_1_beq),
    .bgtz(andlogic_1_bgtz), .blez(andlogic_1_blez), .bne(andlogic_1_bne), .j(andlogic_1_j),
    .jal(andlogic_1_jal), .lui(andlogic_1_lui), .lw(andlogic_1_lw), .ori(andlogic_1_ori),
    .slti(andlogic_1_slti), .sltiu(andlogic_1_sltiu), .sw(andlogic_1_sw), .xori(andlogic_1_xori),
    .add(andlogic_1_add), .addu(andlogic_1_addu), .\and (andlogic_1_and), .div(andlogic_1_div),
    .divu(andlogic_1_divu), .jalr(andlogic_1_jalr), .jr(andlogic_1_jr), .mfhi(andlogic_1_mfhi),
    .mflo(andlogic_1_mflo), .mthi(andlogic_1_mthi), .mtlo(andlogic_1_mtlo), .mult(andlogic_1_mult),
    .multu(andlogic_1_multu), .\nor (andlogic_1_nor), .\or (andlogic_1_or), .sll(andlogic_1_sll),
    .sllv(andlogic_1_sllv), .slt(andlogic_1_slt), .sltu(andlogic_1_sltu), .sra(andlogic_1_sra),
    .srav(andlogic_1_srav), .srl(andlogic_1_srl), .srlv(andlogic_1_srlv), .sub(andlogic_1_sub),
    .subu(andlogic_1_subu), .\xor (andlogic_1_xor), .bgez(andlogic_1_bgez), .bgezal(andlogic_1_bgezal),
    .bltz(andlogic_1_bltz), .bltzal(andlogic_1_bltzal), .SRF_ctrl(SRF_ctrl), .ALU_B_select(ALU_B_select),
    .ALU_A_select(ALU_A_select), .ALU_W_select(ALU_W_select), .addr_select(addr_select),
    .SRF_read_select(SRF_read_select), .GRF_write_data_select(GRF_write_data_select),
    .GRF_write_addr_select(GRF_write_addr_select), .grf_write_enable(grf_write_enable),
    .EXT_signed(EXT_signed), .ALU_ctrl(ALU_ctrl), .ALU_sign_compare(ALU_sign_compare), .DM_write(DM_write),
    .DM_read(DM_read), .jump_control(jump_control), .beq_2(orlogic_1_beq_2), .bgtz_2(orlogic_1_bgtz_2),
    .blez_2(orlogic_1_blez_2), .bne_2(orlogic_1_bne_2), .j_2(orlogic_1_j_2), .jal_2(orlogic_1_jal_2),
    .jalr_2(orlogic_1_jalr_2), .jr_2(orlogic_1_jr_2), .bgez_2(orlogic_1_bgez_2),
    .bgezal_2(orlogic_1_bgezal_2), .bltz_2(orlogic_1_bltz_2), .bltzal_2(orlogic_1_bltzal_2));
  JumpController jumpcontroller_1 (
    .beq(orlogic_1_beq_2), .bgtz(orlogic_1_bgtz_2), .blez(orlogic_1_blez_2), .bne(orlogic_1_bne_2),
    .j(orlogic_1_j_2), .jal(orlogic_1_jal_2), .jalr(orlogic_1_jalr_2), .jr(orlogic_1_jr_2),
    .bgez(orlogic_1_bgez_2), .bgezal(orlogic_1_bgezal_2), .bltz(orlogic_1_bltz_2),
    .bltzal(orlogic_1_bltzal_2), .out_13(cmp_select));
endmodule

module AndLogic (
  input  [5:0] OperationCode,
  input  [5:0] Function,
  input  [4:0] extra,
  output addi,
  output addiu,
  output andi,
  output beq,
  output bgtz,
  output blez,
  output bne,
  output j,
  output jal,
  output lui,
  output lw,
  output ori,
  output slti,
  output sltiu,
  output sw,
  output xori,
  output add,
  output addu,
  output \and ,
  output div,
  output divu,
  output jalr,
  output jr,
  output mfhi,
  output mflo,
  output mthi,
  output mtlo,
  output mult,
  output multu,
  output \nor ,
  output \or ,
  output sll,
  output sllv,
  output slt,
  output sltu,
  output sra,
  output srav,
  output srl,
  output srlv,
  output sub,
  output subu,
  output \xor ,
  output bgez,
  output bgezal,
  output bltz,
  output bltzal
);

  wire andlogic_operationcodedetector_1_extra, andlogic_operationcodedetector_1_special;

  AndLogic__OperationCodeDetector andlogic_operationcodedetector_1 (
    .opcode(OperationCode), .special(andlogic_operationcodedetector_1_special),
    .extra(andlogic_operationcodedetector_1_extra), .addi(addi), .addiu(addiu), .andi(andi), .beq(beq),
    .bgtz(bgtz), .blez(blez), .bne(bne), .j(j), .jal(jal), .lui(lui), .lw(lw), .ori(ori), .slti(slti),
    .sltiu(sltiu), .sw(sw), .xori(xori));
  AddLogic__FuncrionDetector addlogic_funcriondetector_1 (
    .funct(Function), .special(andlogic_operationcodedetector_1_special), .add(add), .addu(addu),
    .\and (\and ), .div(div), .divu(divu), .jalr(jalr), .jr(jr), .mfhi(mfhi), .mflo(mflo), .mthi(mthi),
    .mtlo(mtlo), .mult(mult), .multu(multu), .\nor (\nor ), .\or (\or ), .sll(sll), .sllv(sllv), .slt(slt),
    .sltu(sltu), .sra(sra), .srav(srav), .srl(srl), .srlv(srlv), .sub(sub), .subu(subu), .\xor (\xor ));
  AndLogic__extra andlogic_extra_1 (
    .extra(extra), .is_extra(andlogic_operationcodedetector_1_extra), .bgez(bgez), .bgezal(bgezal),
    .bltz(bltz), .bltzal(bltzal));
endmodule

module AndLogic__OperationCodeDetector (
  input  [5:0] opcode,
  output addi,
  output addiu,
  output andi,
  output beq,
  output bgtz,
  output blez,
  output bne,
  output j,
  output jal,
  output lui,
  output lw,
  output ori,
  output slti,
  output sltiu,
  output sw,
  output xori,
  output special,
  output extra
);

  wire not_1_out, not_2_out, not_3_out, not_4_out, not_5_out, not_6_out;

  not not_1 (not_1_out, opcode[0]);
  not not_2 (not_2_out, opcode[3]);
  not not_3 (not_3_out, opcode[2]);
  not not_4 (not_4_out, opcode[1]);
  not not_5 (not_5_out, opcode[5]);
  not not_6 (not_6_out, opcode[4]);
  and and_1 (addi, not_1_out, not_4_out, not_3_out, opcode[3], not_6_out, not_5_out);
  and and_2 (addiu, opcode[0], not_4_out, not_3_out, opcode[3], not_6_out, not_5_out);
  and and_3 (andi, not_1_out, not_4_out, opcode[2], opcode[3], not_6_out, not_5_out);
  and and_4 (beq, not_1_out, not_4_out, opcode[2], not_2_out, not_6_out, not_5_out);
  and and_5 (bgtz, opcode[0], opcode[1], opcode[2], not_2_out, not_6_out, not_5_out);
  and and_6 (blez, not_1_out, opcode[1], opcode[2], not_2_out, not_6_out, not_5_out);
  and and_7 (bne, opcode[0], not_4_out, opcode[2], not_2_out, not_6_out, not_5_out);
  and and_8 (j, not_1_out, opcode[1], not_3_out, not_2_out, not_6_out, not_5_out);
  and and_9 (jal, opcode[0], opcode[1], not_3_out, not_2_out, not_6_out, not_5_out);
  and and_10 (lui, opcode[0], opcode[1], opcode[2], opcode[3], not_6_out, not_5_out);
  and and_11 (lw, opcode[0], opcode[1], not_3_out, not_2_out, not_6_out, opcode[5]);
  and and_12 (ori, opcode[0], not_4_out, opcode[2], opcode[3], not_6_out, not_5_out);
  and and_13 (slti, not_1_out, opcode[1], not_3_out, opcode[3], not_6_out, not_5_out);
  and and_14 (sltiu, opcode[0], opcode[1], not_3_out, opcode[3], not_6_out, not_5_out);
  and and_15 (sw, opcode[0], opcode[1], not_3_out, opcode[3], not_6_out, opcode[5]);
  and and_16 (xori, not_1_out, opcode[1], opcode[2], opcode[3], not_6_out, not_5_out);
  and and_17 (special, not_1_out, not_4_out, not_3_out, not_2_out, not_6_out, not_5_out);
  and and_18 (extra, opcode[0], not_4_out, not_3_out, not_2_out, not_6_out, not_5_out);
endmodule

module AddLogic__FuncrionDetector (
  input  special,
  input  [5:0] funct,
  output add,
  output addu,
  output \and ,
  output div,
  output divu,
  output jalr,
  output jr,
  output mfhi,
  output mflo,
  output mthi,
  output mtlo,
  output mult,
  output multu,
  output \nor ,
  output \or ,
  output sll,
  output sllv,
  output slt,
  output sltu,
  output sra,
  output srav,
  output srl,
  output srlv,
  output sub,
  output subu,
  output \xor 
);

  wire not_1_out, not_2_out, not_3_out, not_4_out, not_5_out, not_6_out;

  not not_1 (not_1_out, funct[1]);
  not not_2 (not_2_out, funct[0]);
  not not_3 (not_3_out, funct[2]);
  not not_4 (not_4_out, funct[5]);
  not not_5 (not_5_out, funct[4]);
  not not_6 (not_6_out, funct[3]);
  and and_1 (add, special, not_2_out, not_1_out, not_3_out, not_6_out, not_5_out, funct[5]);
  and and_2 (addu, special, funct[0], not_1_out, not_3_out, not_6_out, not_5_out, funct[5]);
  and and_3 (\and , special, not_2_out, not_1_out, funct[2], not_6_out, not_5_out, funct[5]);
  and and_4 (div, special, not_2_out, funct[1], not_3_out, funct[3], funct[4], not_4_out);
  and and_5 (divu, special, funct[0], funct[1], not_3_out, funct[3], funct[4], not_4_out);
  and and_6 (jalr, special, funct[0], not_1_out, not_3_out, funct[3], not_5_out, not_4_out);
  and and_7 (jr, special, not_2_out, not_1_out, not_3_out, funct[3], not_5_out, not_4_out);
  and and_8 (mfhi, special, not_2_out, not_1_out, not_3_out, not_6_out, funct[4], not_4_out);
  and and_9 (mflo, special, not_2_out, funct[1], not_3_out, not_6_out, funct[4], not_4_out);
  and and_10 (mthi, special, funct[0], not_1_out, not_3_out, not_6_out, funct[4], not_4_out);
  and and_11 (mtlo, special, funct[0], funct[1], not_3_out, not_6_out, funct[4], not_4_out);
  and and_12 (mult, special, not_2_out, not_1_out, not_3_out, funct[3], funct[4], not_4_out);
  and and_13 (multu, special, funct[0], not_1_out, not_3_out, funct[3], funct[4], not_4_out);
  and and_14 (\nor , special, funct[0], funct[1], funct[2], not_6_out, not_5_out, funct[5]);
  and and_15 (\or , special, funct[0], not_1_out, funct[2], not_6_out, not_5_out, funct[5]);
  and and_16 (sll, special, not_2_out, not_1_out, not_3_out, not_6_out, not_5_out, not_4_out);
  and and_17 (sllv, special, not_2_out, not_1_out, funct[2], not_6_out, not_5_out, not_4_out);
  and and_18 (slt, special, not_2_out, funct[1], not_3_out, funct[3], not_5_out, funct[5]);
  and and_19 (sltu, special, funct[0], funct[1], not_3_out, funct[3], not_5_out, funct[5]);
  and and_20 (sra, special, funct[0], funct[1], not_3_out, not_6_out, not_5_out, not_4_out);
  and and_21 (srav, special, funct[0], funct[1], funct[2], not_6_out, not_5_out, not_4_out);
  and and_22 (srl, special, not_2_out, funct[1], not_3_out, not_6_out, not_5_out, not_4_out);
  and and_23 (srlv, special, not_2_out, funct[1], funct[2], not_6_out, not_5_out, not_4_out);
  and and_24 (sub, special, not_2_out, funct[1], not_3_out, not_6_out, not_5_out, funct[5]);
  and and_25 (subu, special, funct[0], funct[1], not_3_out, not_6_out, not_5_out, funct[5]);
  and and_26 (\xor , special, not_2_out, funct[1], funct[2], not_6_out, not_5_out, funct[5]);
endmodule

module OrLogic (
  input  addi,
  input  addiu,
  input  andi,
  input  beq,
  input  bgtz,
  input  blez,
  input  bne,
  input  j,
  input  jal,
  input  lui,
  input  lw,
  input  ori,
  input  slti,
  input  sltiu,
  input  sw,
  input  xori,
  input  add,
  input  addu,
  input  \and ,
  input  div,
  input  divu,
  input  jalr,
  input  jr,
  input  mfhi,
  input  mflo,
  input  mthi,
  input  mtlo,
  input  mult,
  input  multu,
  input  \nor ,
  input  \or ,
  input  sll,
  input  sllv,
  input  slt,
  input  sltu,
  input  sra,
  input  srav,
  input  srl,
  input  srlv,
  input  sub,
  input  subu,
  input  \xor ,
  input  bgez,
  input  bgezal,
  input  bltz,
  input  bltzal,
  output [3:0] SRF_ctrl,
  output [1:0] ALU_B_select,
  output [1:0] ALU_A_select,
  output [1:0] ALU_W_select,
  output [1:0] addr_select,
  output SRF_read_select,
  output [2:0] GRF_write_data_select,
  output [1:0] GRF_write_addr_select,
  output grf_write_enable,
  output EXT_signed,
  output [3:0] ALU_ctrl,
  output ALU_sign_compare,
  output DM_write,
  output DM_read,
  output [1:0] jump_control,
  output beq_2,
  output bgtz_2,
  output blez_2,
  output bne_2,
  output j_2,
  output jal_2,
  output jalr_2,
  output jr_2,
  output bgez_2,
  output bgezal_2,
  output bltz_2,
  output bltzal_2
);

  wire ALU_add_out, ALU_nor_out, ALU_or_out, ALU_sll_out, ALU_sra_out, ALU_srl_out, ALU_sub_out, ALU_xor_out,
       div_out, read_SRF_out, set_bit_out, write_ra_out, write_rt_out;

  or u_div (div_out, div, divu);
  or write_ra (write_ra_out, jal, jalr, bgezal, bltzal);
  or read_SRF (read_SRF_out, mfhi, mflo);
  or set_bit (set_bit_out, slti, sltiu, slt, sltu);
  or write_rt (write_rt_out, addi, lui, addiu, lw, andi, ori, slti, xori, sltiu);
  or write_ra_2 (GRF_write_addr_select[1], jal, jalr, bgezal, bltzal);
  or write_grf (grf_write_enable, addi, addiu, andi, jal, lui, lw, ori, slti, sltiu, xori, add, addu, \and , jalr, mfhi, mflo, \nor , \or , sll, sllv, slt, sltu, sra, srav, srl, srlv, sub, subu, \xor , bgezal, bltzal);
  or signed_extend (EXT_signed, beq, bgez, bgtz, bgezal, blez, bltz, bne, bltzal, addi, addiu, slti, lw, sltiu, sw);
  or ALU_or (ALU_or_out, ori, \or );
  buf ALU_nor (ALU_nor_out, \nor );  // OR_Gate
  or ALU_xor (ALU_xor_out, xori, \xor );
  or ALU_add (ALU_add_out, addi, lw, addiu, add, sw, addu);
  or ALU_sub (ALU_sub_out, sub, subu);
  or ALU_sll (ALU_sll_out, sll, lui, sllv);
  or ALU_srl (ALU_srl_out, srl, srlv);
  or ALU_sra (ALU_sra_out, sra, srav);
  or signed_cmp (ALU_sign_compare, beq, sltiu, bgtz, slt, blez, bgez, bne, bgezal, bltzal, bltz);
  or or_1 (SRF_ctrl[0], mtlo, div_out);
  or or_2 (SRF_ctrl[1], div_out, mthi);
  or \signed  (SRF_ctrl[2], divu, multu);
  or SRF_en (SRF_ctrl[3], div, mthi, divu, mult, mtlo, multu);
  or imm (ALU_B_select[0], addi, addiu, andi, ori, lw, slti, sltiu, sw, xori);
  or cmp0 (ALU_B_select[1], blez, bgtz, bgez, bltz, bgezal, bltzal);
  or rt (ALU_A_select[1], sll, sra, sllv, srl, srav, srlv);
  or sim (ALU_W_select[0], sll, sra, srl);
  or sv (ALU_W_select[1], sllv, srav, srlv);
  or u_j (addr_select[0], j, jal);
  or u_jr (addr_select[1], jalr, jr);
  or or_3 (GRF_write_addr_select[0], write_rt_out, GRF_write_addr_select[1]);
  or b (jump_control[0], beq, bne, bgtz, blez, bgez, bltz, bgezal, bltzal);
  or u_j_2 (jump_control[1], j, jal, jalr, jr);
  or or_4 (GRF_write_data_select[0], write_ra_out, read_SRF_out);
  or or_5 (GRF_write_data_select[1], lw, read_SRF_out);
  buf or_6 (GRF_write_data_select[2], set_bit_out);  // OR_Gate
  or or_7 (ALU_ctrl[0], ALU_or_out, ALU_xor_out, ALU_sub_out, ALU_srl_out);
  or or_8 (ALU_ctrl[1], ALU_nor_out, ALU_xor_out, ALU_sll_out, ALU_srl_out);
  or or_9 (ALU_ctrl[2], ALU_add_out, ALU_sub_out, ALU_sll_out, ALU_srl_out);
  buf or_10 (ALU_ctrl[3], ALU_sra_out);  // OR_Gate

  assign ALU_A_select[0] = lui;
  assign beq_2 = beq;
  assign bgez_2 = bgez;
  assign bgezal_2 = bgezal;
  assign bgtz_2 = bgtz;
  assign blez_2 = blez;
  assign bltz_2 = bltz;
  assign bltzal_2 = bltzal;
  assign bne_2 = bne;
  assign DM_read = lw;
  assign DM_write = sw;
  assign j_2 = j;
  assign jal_2 = jal;
  assign jalr_2 = jalr;
  assign jr_2 = jr;
  assign SRF_read_select = mfhi;

  // Other names for the same wires on the sheet: blezal = bltzal
endmodule

module AndLogic__extra (
  input  is_extra,
  input  [4:0] extra,
  output bgez,
  output bgezal,
  output bltz,
  output bltzal
);

  wire and_1_out, and_2_out, and_3_out, and_4_out, not_1_out, not_2_out, not_3_out, not_4_out, not_5_out;

  not not_1 (not_1_out, extra[1]);
  not not_2 (not_2_out, extra[0]);
  not not_3 (not_3_out, extra[2]);
  not not_4 (not_4_out, extra[3]);
  not not_5 (not_5_out, extra[4]);
  and and_1 (and_1_out, extra[0], not_1_out, not_3_out, not_4_out, not_5_out);
  and and_2 (and_2_out, extra[0], not_1_out, not_3_out, not_4_out, extra[4]);
  and and_3 (and_3_out, not_2_out, not_1_out, not_3_out, not_4_out, not_5_out);
  and and_4 (and_4_out, not_2_out, not_1_out, not_3_out, not_4_out, extra[4]);
  and and_5 (bgez, is_extra, and_1_out);
  and and_6 (bgezal, is_extra, and_2_out);
  and and_7 (bltz, is_extra, and_3_out);
  and and_8 (bltzal, is_extra, and_4_out);
endmodule

module JumpController (
  input  beq,
  input  bgtz,
  input  blez,
  input  bne,
  input  j,
  input  jal,
  input  jalr,
  input  jr,
  input  bgez,
  input  bgezal,
  input  bltz,
  input  bltzal,
  output [2:0] out_13
);

  wire eq_out, ge_out, gt_out, le_out, ne_2_out, ne_out;

  // OR_Gate lt has open pins: in0=bltz, in1=bltzal, out=open
  buf le (le_out, blez);  // OR_Gate
  buf eq (eq_out, beq);  // OR_Gate
  or ge (ge_out, bgez, bgezal);
  buf gt (gt_out, bgtz);  // OR_Gate
  buf ne (ne_out, bne);  // OR_Gate
  or ne_2 (ne_2_out, j, jal, jalr, jr);
  or or_1 (out_13[0], le_out, ge_out, ne_out);
  or or_2 (out_13[1], eq_out, ge_out, ne_2_out);
  or or_3 (out_13[2], gt_out, ne_out, ne_2_out);
endmodule
