// Logisim project DM.circ as structural Verilog: 1 circuit, main circuit DM
module DM (
  input  [31:0] Addr,
  input  [31:0] Data,
  input  S,
  input  L,
  input  C,
  input  Clock,
  output [31:0] Output
);

  RAM #(.addrWidth(12), .dataWidth(32), .bus("separate")) ram_1 (
    .addr(Addr[13:2]), .din(Data), .data(Output), .str(S), .clk(Clock), .ld(L), .clr(C));  // open: sel
endmodule
