// Logisim project EXT.circ as structural Verilog: 1 circuit, main circuit EXT
module EXT (
  input  Signed,
  input  [15:0] Src,
  output [31:0] out_3
);

  and and_1 (out_3[31], Signed, Src[15]);

  assign out_3[30:0] = {{15{out_3[31]}}, Src};
endmodule
