// Logisim project GRF.circ as structural Verilog: 1 circuit, main circuit GRF
module GRF (
  input  [31:0] Input,
  input  [4:0] read_addr0,
  input  [4:0] read_addr1,
  input  write_enable,
  input  [4:0] write_addr,
  input  Clock,
  input  Reset,
  output [31:0] out_8,
  output [31:0] out_9
);

  wire decoder_1_out0, decoder_1_out1, decoder_1_out2, decoder_1_out3, decoder_1_out4, decoder_1_out5,
       decoder_1_out6, decoder_1_out7, decoder_1_out8, decoder_1_out9, decoder_1_out10, decoder_1_out11,
       decoder_1_out12, decoder_1_out13, decoder_1_out14, decoder_1_out15, decoder_1_out16, decoder_1_out17,
       decoder_1_out18, decoder_1_out19, decoder_1_out20, decoder_1_out21, decoder_1_out22, decoder_1_out23,
       decoder_1_out24, decoder_1_out25, decoder_1_out26, decoder_1_out27, decoder_1_out28, decoder_1_out29,
       decoder_1_out30, decoder_1_out31;
  wire [31:0] a0_q, a1_q, a2_q, a3_q, at_q, fp_q, gp_q, k0_q, k1_q, n32_bit_adder_1_s, n32_bit_adder_2_s,
       ra_q, s0_q, s1_q, s2_q, s3_q, s4_q, s5_q, s6_q, s7_q, sp_q, t0_q, t1_q, t2_q, t3_q, t4_q, t5_q, t6_q,
       t7_q, t8_q, t9_q, v0_q, v1_q, zero_q;

  Decoder #(.select(5), .disabled(0)) decoder_1 (
    .out0(decoder_1_out0), .out1(decoder_1_out1), .out2(decoder_1_out2), .out3(decoder_1_out3),
    .out4(decoder_1_out4), .out5(decoder_1_out5), .out6(decoder_1_out6), .out7(decoder_1_out7),
    .out8(decoder_1_out8), .out9(decoder_1_out9), .out10(decoder_1_out10), .out11(decoder_1_out11),
    .out12(decoder_1_out12), .out13(decoder_1_out13), .out14(decoder_1_out14), .out15(decoder_1_out15),
    .out16(decoder_1_out16), .out17(decoder_1_out17), .out18(decoder_1_out18), .out19(decoder_1_out19),
    .out20(decoder_1_out20), .out21(decoder_1_out21), .out22(decoder_1_out22), .out23(decoder_1_out23),
    .out24(decoder_1_out24), .out25(decoder_1_out25), .out26(decoder_1_out26), .out27(decoder_1_out27),
    .out28(decoder_1_out28), .out29(decoder_1_out29), .out30(decoder_1_out30), .out31(decoder_1_out31),
    .sel(write_addr), .en(write_enable));
  _32_bit_adder u_32_bit_adder_1 (.A(Input), .B(32'hffffd004), .S(n32_bit_adder_1_s));  // open: Cin, Cout
  Register #(.width(32)) zero (.en(decoder_1_out0), .Q(zero_q), .clk(Clock), .clr(Reset));  // open: D
  Register #(.width(32)) at (.D(Input), .en(decoder_1_out1), .Q(at_q), .clk(Clock), .clr(Reset));
  Register #(.width(32)) v0 (.D(Input), .en(decoder_1_out2), .Q(v0_q), .clk(Clock), .clr(Reset));
  Register #(.width(32)) v1 (.D(Input), .en(decoder_1_out3), .Q(v1_q), .clk(Clock), .clr(Reset));
  Register #(.width(32)) a0 (.D(Input), .en(decoder_1_out4), .Q(a0_q), .clk(Clock), .clr(Reset));
  Register #(.width(32)) a1 (.D(Input), .en(decoder_1_out5), .Q(a1_q), .clk(Clock), .clr(Reset));
  Register #(.width(32)) a2 (.D(Input), .en(decoder_1_out6), .Q(a2_q), .clk(Clock), .clr(Reset));
  Register #(.width(32)) a3 (.D(Input), .en(decoder_1_out7), .Q(a3_q), .clk(Clock), .clr(Reset));
  Register #(.width(32)) t0 (.D(Input), .en(decoder_1_out8), .Q(t0_q), .clk(Clock), .clr(Reset));
  Register #(.width(32)) t1 (.D(Input), .en(decoder_1_out9), .Q(t1_q), .clk(Clock), .clr(Reset));
  Register #(.width(32)) t2 (.D(Input), .en(decoder_1_out10), .Q(t2_q), .clk(Clock), .clr(Reset));
  Register #(.width(32)) t3 (.D(Input), .en(decoder_1_out11), .Q(t3_q), .clk(Clock), .clr(Reset));
  Register #(.width(32)) t4 (.D(Input), .en(decoder_1_out12), .Q(t4_q), .clk(Clock), .clr(Reset));
  Register #(.width(32)) t5 (.D(Input), .en(decoder_1_out13), .Q(t5_q), .clk(Clock), .clr(Reset));
  Register #(.width(32)) t6 (.D(Input), .en(decoder_1_out14), .Q(t6_q), .clk(Clock), .clr(Reset));
  Register #(.width(32)) t7 (.D(Input), .en(decoder_1_out15), .Q(t7_q), .clk(Clock), .clr(Reset));
  Register #(.width(32)) s0 (.D(Input), .en(decoder_1_out16), .Q(s0_q), .clk(Clock), .clr(Reset));
  Register #(.width(32)) s1 (.D(Input), .en(decoder_1_out17), .Q(s1_q), .clk(Clock), .clr(Reset));
  Register #(.width(32)) s2 (.D(Input), .en(decoder_1_out18), .Q(s2_q), .clk(Clock), .clr(Reset));
  Register #(.width(32)) s3 (.D(Input), .en(decoder_1_out19), .Q(s3_q), .clk(Clock), .clr(Reset));
  Register #(.width(32)) s4 (.D(Input), .en(decoder_1_out20), .Q(s4_q), .clk(Clock), .clr(Reset));
  Register #(.width(32)) s5 (.D(Input), .en(decoder_1_out21), .Q(s5_q), .clk(Clock), .clr(Reset));
  Register #(.width(32)) s6 (.D(Input), .en(decoder_1_out22), .Q(s6_q), .clk(Clock), .clr(Reset));
  Register #(.width(32)) s7 (.D(Input), .en(decoder_1_out23), .Q(s7_q), .clk(Clock), .clr(Reset));
  Register #(.width(32)) t8 (.D(Input), .en(decoder_1_out24), .Q(t8_q), .clk(Clock), .clr(Reset));
  Register #(.width(32)) t9 (.D(Input), .en(decoder_1_out25), .Q(t9_q), .clk(Clock), .clr(Reset));
  Register #(.width(32)) k0 (.D(Input), .en(decoder_1_out26), .Q(k0_q), .clk(Clock), .clr(Reset));
  Register #(.width(32)) k1 (.D(Input), .en(decoder_1_out27), .Q(k1_q), .clk(Clock), .clr(Reset));
  Register #(.width(32)) gp (.D(Input), .en(decoder_1_out28), .Q(gp_q), .clk(Clock), .clr(Reset));
  Register #(.width(32)) sp (.D(n32_bit_adder_1_s), .en(decoder_1_out29), .Q(sp_q), .clk(Clock), .clr(Reset));
  Register #(.width(32)) fp (.D(Input), .en(decoder_1_out30), .Q(fp_q), .clk(Clock), .clr(Reset));
  Register #(.width(32)) ra (.D(Input), .en(decoder_1_out31), .Q(ra_q), .clk(Clock), .clr(Reset));
  _32_bit_adder u_32_bit_adder_2 (.A(sp_q), .B(32'h2ffc), .S(n32_bit_adder_2_s));  // open: Cin, Cout
  Multiplexer #(.select(5), .width(32), .enable("false")) multiplexer_1 (
    .in0(zero_q), .in1(at_q), .in2(v0_q), .in3(v1_q), .in4(a0_q), .in5(a1_q), .in6(a2_q), .in7(a3_q),
    .in8(t0_q), .in9(t1_q), .in10(t2_q), .in11(t3_q), .in12(t4_q), .in13(t5_q), .in14(t6_q), .in15(t7_q),
    .in16(s0_q), .in17(s1_q), .in18(s2_q), .in19(s3_q), .in20(s4_q), .in21(s5_q), .in22(s6_q), .in23(s7_q),
    .in24(t8_q), .in25(t9_q), .in26(k0_q), .in27(k1_q), .in28(gp_q), .in29(n32_bit_adder_2_s), .in30(fp_q),
    .in31(ra_q), .out(out_8), .sel(read_addr0));
  Multiplexer #(.select(5), .width(32), .enable("false")) multiplexer_2 (
    .in0(zero_q), .in1(at_q), .in2(v0_q), .in3(v1_q), .in4(a0_q), .in5(a1_q), .in6(a2_q), .in7(a3_q),
    .in8(t0_q), .in9(t1_q), .in10(t2_q), .in11(t3_q), .in12(t4_q), .in13(t5_q), .in14(t6_q), .in15(t7_q),
    .in16(s0_q), .in17(s1_q), .in18(s2_q), .in19(s3_q), .in20(s4_q), .in21(s5_q), .in22(s6_q), .in23(s7_q),
    .in24(t8_q), .in25(t9_q), .in26(k0_q), .in27(k1_q), .in28(gp_q), .in29(n32_bit_adder_2_s), .in30(fp_q),
    .in31(ra_q), .out(out_9), .sel(read_addr1));

  // Notes on the sheet:
  //   write_enable: pull=down
  //   Reset: pull=down
endmodule
