// Logisim project IFU.circ as structural Verilog: 1 circuit, main circuit IFU
module IFU (
  input  [1:0] PC_select,
  input  Clock,
  input  Reset,
  input  [31:0] \input ,
  output [31:0] Instruction,
  output [31:0] PC_4
);

  wire [31:0] multiplexer_1_out, n32_bit_adder_1_s, n32_bit_adder_2_s, n32_bit_adder_3_s, PC_q;

  _32_bit_adder u_32_bit_adder_1 (.A(\input ), .B(32'hffffd000), .S(n32_bit_adder_1_s));  // open: Cin, Cout
  Multiplexer #(.select(2), .width(32), .enable("false")) multiplexer_1 (
    .in0(n32_bit_adder_2_s), .in1(n32_bit_adder_3_s), .in2(n32_bit_adder_1_s), .out(multiplexer_1_out),
    .sel(PC_select));  // open: in3
  Register #(.width(32)) PC (.D(multiplexer_1_out), .Q(PC_q), .clk(Clock), .clr(Reset));  // open: en
  _32_bit_adder u_32_bit_adder_2 (.A(PC_q), .B(32'h4), .S(n32_bit_adder_2_s));  // open: Cin, Cout
  _32_bit_adder u_32_bit_adder_3 (.A(n32_bit_adder_2_s), .B(\input ), .S(n32_bit_adder_3_s));  // open: Cin, Cout
  _32_bit_adder u_32_bit_adder_4 (.A(n32_bit_adder_2_s), .B(32'h3000), .S(PC_4));  // open: Cin, Cout
  ROM #(.addrWidth(10), .dataWidth(32)) rom_1 (.addr(PC_q[11:2]), .data(Instruction));  // open: sel

  // Notes on the sheet:
  //   contents of rom_1 (hex, n*v repeats v):
  //   24080001 ac080000 24100004 2412000a 2411000f 24080001 24090000 240b0000 8d2a0000 1480019 5012
  //   14b5020 152001a 5010 5812 ad2a0000 21290004 130082a 1420fff5 11600009 172001a 5012 5810 ad2b0000
  //   22100004 11400003 21290004 22100004 ad2a0000 21080001 228082a 1020ffe6 2004020 2108fffc 8d090000
  //   2108fffc 501fffd 8000c25
endmodule
