// Logisim project InstructionSplitter.circ as structural Verilog: 1 circuit, main circuit InstructionSplitter
module InstructionSplitter (
  input  [31:0] Instruction,
  output [25:0] address,
  output [15:0] offset,
  output [5:0] funct,
  output [4:0] shamt,
  output [4:0] rd,
  output [4:0] rt,
  output [4:0] rs,
  output [5:0] opcode
);


  assign address = Instruction[25:0];
  assign funct = Instruction[5:0];
  assign offset = Instruction[15:0];
  assign opcode = Instruction[31:26];
  assign rd = Instruction[15:11];
  assign rs = Instruction[25:21];
  assign rt = Instruction[20:16];
  assign shamt = Instruction[10:6];
endmodule
