// Logisim project SRF.circ as structural Verilog: 4 circuits, main circuit SRF
module SRF (
  input  [3:0] control,
  input  [31:0] A,
  input  [31:0] B,
  input  clock,
  input  reset,
  output [31:0] LO,
  output [31:0] HI
);

  wire srf_control_1_hi_enable, srf_control_1_lo_enable, srf_control_1_signed;
  wire [1:0] srf_control_1_function;
  wire [31:0] divider_1_out, divider_1_rem, multiplexer_1_out, multiplexer_2_out, multiplexer_3_out,
       multiplexer_4_out, multiplexer_5_out, multiplexer_6_out, multiplier_1_cout, multiplier_1_out,
       signed_div_1_hi, signed_div_1_lo, unsigned_multi_1_hi, unsigned_multi_1_lo;

  unsigned_multi unsigned_multi_1 (.A(A), .B(B), .LO(unsigned_multi_1_lo), .HI(unsigned_multi_1_hi));
  Multiplier #(.width(32)) multiplier_1 (.a(A), .b(B), .out(multiplier_1_out), .cout(multiplier_1_cout));  // open: cin
  Divider #(.width(32)) divider_1 (.a(A), .b(B), .out(divider_1_out), .rem(divider_1_rem));  // open: upper
  signed_div signed_div_1 (.A(A), .B(B), .LO(signed_div_1_lo), .HI(signed_div_1_hi));
  SRF_control srf_control_1 (
    .in_1(control), .\signed (srf_control_1_signed), .\function (srf_control_1_function),
    .LO_enable(srf_control_1_lo_enable), .HI_enable(srf_control_1_hi_enable));
  Multiplexer #(.width(32), .enable("false")) multiplexer_1 (
    .in0(unsigned_multi_1_lo), .in1(multiplier_1_out), .out(multiplexer_1_out), .sel(srf_control_1_signed));
  Multiplexer #(.width(32), .enable("false")) multiplexer_2 (
    .in0(unsigned_multi_1_hi), .in1(multiplier_1_cout), .out(multiplexer_2_out), .sel(srf_control_1_signed));
  Multiplexer #(.width(32), .enable("false")) multiplexer_3 (
    .in0(divider_1_out), .in1(signed_div_1_lo), .out(multiplexer_3_out), .sel(srf_control_1_signed));
  Multiplexer #(.width(32), .enable("false")) multiplexer_4 (
    .in0(divider_1_rem), .in1(signed_div_1_hi), .out(multiplexer_4_out), .sel(srf_control_1_signed));
  Multiplexer #(.select(2), .width(32), .enable("false")) multiplexer_5 (
    .in0(multiplexer_1_out), .in1(A), .in2(A), .in3(multiplexer_3_out), .out(multiplexer_5_out),
    .sel(srf_control_1_function));
  Multiplexer #(.select(2), .width(32), .enable("false")) multiplexer_6 (
    .in0(multiplexer_2_out), .in1(A), .in2(A), .in3(multiplexer_4_out), .out(multiplexer_6_out),
    .sel(srf_control_1_function));
  Register #(.width(32)) u_LO (.D(multiplexer_5_out), .en(srf_control_1_lo_enable), .Q(LO), .clk(clock), .clr(reset));
  Register #(.width(32)) u_HI (.D(multiplexer_6_out), .en(srf_control_1_hi_enable), .Q(HI), .clk(clock), .clr(reset));
endmodule

module unsigned_multi (
  input  [31:0] A,
  input  [31:0] B,
  output [31:0] LO,
  output [31:0] HI
);

  wire adder_1_cout, adder_2_cout;
  wire [30:0] and_3_out, multiplier_1_cout, multiplier_1_out;
  wire [30:30] and_1_out;
  wire [31:0] adder_1_out;
  wire [31:1] and_2_out;

  Multiplier #(.width(31)) multiplier_1 (
    .a(A[31:1]), .b(B[31:1]), .out(multiplier_1_out), .cin({31{and_1_out[30]}}), .cout(multiplier_1_cout));
  and and_1 (and_1_out[30], B[0], A[0]);
  Adder #(.width(32)) adder_1 (
    .a({and_3_out, 1'b0}), .b({and_2_out, 1'b0}), .out(adder_1_out), .cout(adder_1_cout));  // open: cin
  Adder #(.width(32)) adder_2 (
    .a(adder_1_out), .b({multiplier_1_out[29:0], 2'b00}), .out(LO), .cin(adder_1_cout), .cout(adder_2_cout));
  Adder #(.width(32)) adder_3 (
    .a({multiplier_1_cout, multiplier_1_out[30]}), .b({32{1'b0}}), .out(HI), .cin(adder_2_cout));  // open: cout
  assign and_2_out = B[31:1] & {31{A[0]}};  // AND_Gate and_2, 31 bits wide
  assign and_3_out = A[31:1] & {31{B[0]}};  // AND_Gate and_3, 31 bits wide
endmodule

module signed_div (
  input  [31:0] A,
  input  [31:0] B,
  output [31:0] LO,
  output [31:0] HI
);

  wire xor_1_out;
  wire [31:0] divider_1_out, divider_1_rem, multiplexer_1_out, multiplexer_2_out, negator_1_out,
       negator_2_out, negator_3_out, negator_4_out;

  xor xor_1 (xor_1_out, B[31], A[31]);
  Negator #(.width(32)) negator_1 (.in(A), .out(negator_1_out));
  Negator #(.width(32)) negator_2 (.in(B), .out(negator_2_out));
  Multiplexer #(.width(32), .enable("false")) multiplexer_1 (
    .in0(A), .in1(negator_1_out), .out(multiplexer_1_out), .sel(A[31]));
  Multiplexer #(.width(32), .enable("false")) multiplexer_2 (
    .in0(B), .in1(negator_2_out), .out(multiplexer_2_out), .sel(B[31]));
  Divider #(.width(32)) divider_1 (
    .a(multiplexer_1_out), .b(multiplexer_2_out), .out(divider_1_out), .rem(divider_1_rem));  // open: upper
  Negator #(.width(32)) negator_3 (.in(divider_1_out), .out(negator_3_out));
  Multiplexer #(.width(32), .enable("false")) multiplexer_3 (
    .in0(divider_1_rem), .in1(negator_4_out), .out(HI), .sel(xor_1_out));
  Negator #(.width(32)) negator_4 (.in(divider_1_rem), .out(negator_4_out));
  Multiplexer #(.width(32), .enable("false")) multiplexer_4 (
    .in0(divider_1_out), .in1(negator_3_out), .out(LO), .sel(xor_1_out));
endmodule

module SRF_control (
  input  [3:0] in_1,
  output \signed ,
  output [1:0] \function ,
  output LO_enable,
  output HI_enable
);

  wire or_1_out, or_2_out, xnor_1_out;

  xnor xnor_1 (xnor_1_out, in_1[0], in_1[1]);
  or or_1 (or_1_out, xnor_1_out, in_1[0]);
  and and_1 (LO_enable, in_1[3], or_1_out);
  or or_2 (or_2_out, xnor_1_out, in_1[1]);
  and and_2 (HI_enable, in_1[3], or_2_out);

  assign \function  = in_1[1:0];
  assign \signed  = in_1[2];
endmodule
