// Logisim project Logisim.circ as structural Verilog: 26 circuits, main circuit 1bit_swap
module _1bit_swap (
  input  a,
  input  b,
  input  c,
  output x,
  output y
);

  wire nand_1_out, nand_2_out, nand_3_out, nand_4_out, nand_5_out, nand_6_out, nand_7_out, nand_8_out,
       nand_9_out, nand_11_out, nand_12_out, nand_13_out, nand_14_out, nand_15_out, nand_16_out, nand_17_out,
       nand_18_out, nand_19_out, nand_20_out, nand_21_out, nand_22_out, nand_23_out, nand_24_out;

  nand nand_1 (nand_1_out, c, c);
  nand nand_2 (nand_2_out, a, a);
  nand nand_3 (nand_3_out, b, b);
  nand nand_4 (nand_4_out, b, c);
  nand nand_5 (nand_5_out, a, nand_1_out);
  nand nand_6 (nand_6_out, nand_2_out, b);
  nand nand_7 (nand_7_out, a, nand_3_out);
  nand nand_8 (nand_8_out, a, b);
  nand nand_9 (nand_9_out, a, b);
  nand nand_10 (x, nand_4_out, nand_5_out);
  nand nand_11 (nand_11_out, nand_6_out, nand_6_out);
  nand nand_12 (nand_12_out, c, c);
  nand nand_13 (nand_13_out, nand_7_out, nand_7_out);
  nand nand_14 (nand_14_out, nand_8_out, nand_8_out);
  nand nand_15 (nand_15_out, c, c);
  nand nand_16 (nand_16_out, nand_9_out, nand_9_out);
  nand nand_17 (nand_17_out, nand_11_out, nand_12_out);
  nand nand_18 (nand_18_out, nand_13_out, c);
  nand nand_19 (nand_19_out, nand_14_out, nand_15_out);
  nand nand_20 (nand_20_out, nand_16_out, c);
  nand nand_21 (nand_21_out, nand_17_out, nand_18_out);
  nand nand_22 (nand_22_out, nand_19_out, nand_20_out);
  nand nand_23 (nand_23_out, nand_21_out, nand_21_out);
  nand nand_24 (nand_24_out, nand_22_out, nand_22_out);
  nand nand_25 (y, nand_23_out, nand_24_out);
endmodule

module swap (
  input  I1,
  input  I2,
  input  S,
  output O1,
  output O2
);

  _1bit_swap u_1bit_swap_1 (.a(I1), .b(I2), .c(S), .x(O1), .y(O2));
endmodule

module _4bit_swap (
  input  [3:0] in_1,
  input  [3:0] in_2,
  input  in_3,
  output [3:0] out_4,
  output [3:0] out_5
);

  _1bit_swap u_1bit_swap_1 (.a(in_1[0]), .b(in_2[0]), .c(in_3), .x(out_4[0]), .y(out_5[0]));
  _1bit_swap u_1bit_swap_2 (.a(in_1[1]), .b(in_2[1]), .c(in_3), .x(out_4[1]), .y(out_5[1]));
  _1bit_swap u_1bit_swap_3 (.a(in_1[2]), .b(in_2[2]), .c(in_3), .x(out_4[2]), .y(out_5[2]));
  _1bit_swap u_1bit_swap_4 (.a(in_1[3]), .b(in_2[3]), .c(in_3), .x(out_4[3]), .y(out_5[3]));
endmodule

module _2way_comparer (
  input  Most_Significant_lt,
  input  Most_Significant_eq,
  input  Most_Significant_gt,
  input  Less_Significant_lt,
  input  Less_Significant_eq,
  input  Less_Significant_gt,
  output lt,
  output eq,
  output gt
);

  wire and_1_out, and_3_out;

  and and_1 (and_1_out, Most_Significant_eq, Less_Significant_lt);
  and and_2 (eq, Most_Significant_eq, Less_Significant_eq);
  and and_3 (and_3_out, Most_Significant_eq, Less_Significant_gt);
  or or_1 (lt, Most_Significant_lt, and_1_out);
  or or_2 (gt, Most_Significant_gt, and_3_out);
endmodule

module _1bit_comparer (
  input  in_1,
  input  in_2,
  output out_3,
  output out_4,
  output out_5
);

  wire not_1_out, not_2_out;

  not not_1 (not_1_out, in_1);
  not not_2 (not_2_out, in_2);
  and and_1 (out_3, not_1_out, in_2);
  and and_2 (out_5, in_1, not_2_out);
  xnor xnor_1 (out_4, in_1, in_2);
endmodule

module _2bit_comparer (
  input  [1:0] X,
  input  [1:0] Y,
  output gt,
  output eq,
  output lt
);

  wire n1bit_comparer_1_out_3, n1bit_comparer_1_out_4, n1bit_comparer_1_out_5, n1bit_comparer_2_out_3,
       n1bit_comparer_2_out_4, n1bit_comparer_2_out_5;

  _1bit_comparer u_1bit_comparer_1 (
    .in_1(X[1]), .in_2(Y[1]), .out_3(n1bit_comparer_1_out_3), .out_4(n1bit_comparer_1_out_4),
    .out_5(n1bit_comparer_1_out_5));
  _1bit_comparer u_1bit_comparer_2 (
    .in_1(X[0]), .in_2(Y[0]), .out_3(n1bit_comparer_2_out_3), .out_4(n1bit_comparer_2_out_4),
    .out_5(n1bit_comparer_2_out_5));
  _2way_comparer u_2way_comparer_1 (
    .Most_Significant_lt(n1bit_comparer_1_out_3), .Most_Significant_eq(n1bit_comparer_1_out_4),
    .Most_Significant_gt(n1bit_comparer_1_out_5), .Less_Significant_lt(n1bit_comparer_2_out_3),
    .Less_Significant_eq(n1bit_comparer_2_out_4), .Less_Significant_gt(n1bit_comparer_2_out_5), .lt(gt),
    .eq(eq), .gt(lt));
endmodule

module _3bit_comparer (
  input  [2:0] X,
  input  [2:0] Y,
  output lt,
  output eq,
  output gt
);

  wire n1bit_comparer_1_out_3, n1bit_comparer_1_out_4, n1bit_comparer_1_out_5, n2bit_comparer_1_eq,
       n2bit_comparer_1_gt, n2bit_comparer_1_lt;

  _2bit_comparer u_2bit_comparer_1 (
    .X(X[2:1]), .Y(Y[2:1]), .gt(n2bit_comparer_1_gt), .eq(n2bit_comparer_1_eq), .lt(n2bit_comparer_1_lt));
  _1bit_comparer u_1bit_comparer_1 (
    .in_1(X[0]), .in_2(Y[0]), .out_3(n1bit_comparer_1_out_3), .out_4(n1bit_comparer_1_out_4),
    .out_5(n1bit_comparer_1_out_5));
  _2way_comparer u_2way_comparer_1 (
    .Most_Significant_lt(n2bit_comparer_1_gt), .Most_Significant_eq(n2bit_comparer_1_eq),
    .Most_Significant_gt(n2bit_comparer_1_lt), .Less_Significant_lt(n1bit_comparer_1_out_3),
    .Less_Significant_eq(n1bit_comparer_1_out_4), .Less_Significant_gt(n1bit_comparer_1_out_5), .lt(lt),
    .eq(eq), .gt(gt));
endmodule

module _4bit_comparer (
  input  [3:0] X,
  input  [3:0] Y,
  output lt,
  output eq,
  output gt
);

  wire n2bit_comparer_1_eq, n2bit_comparer_1_gt, n2bit_comparer_1_lt, n2bit_comparer_2_eq,
       n2bit_comparer_2_gt, n2bit_comparer_2_lt;

  _2bit_comparer u_2bit_comparer_1 (
    .X(X[3:2]), .Y(Y[3:2]), .gt(n2bit_comparer_1_gt), .eq(n2bit_comparer_1_eq), .lt(n2bit_comparer_1_lt));
  _2bit_comparer u_2bit_comparer_2 (
    .X(X[1:0]), .Y(Y[1:0]), .gt(n2bit_comparer_2_gt), .eq(n2bit_comparer_2_eq), .lt(n2bit_comparer_2_lt));
  _2way_comparer u_2way_comparer_1 (
    .Most_Significant_lt(n2bit_comparer_1_gt), .Most_Significant_eq(n2bit_comparer_1_eq),
    .Most_Significant_gt(n2bit_comparer_1_lt), .Less_Significant_lt(n2bit_comparer_2_gt),
    .Less_Significant_eq(n2bit_comparer_2_eq), .Less_Significant_gt(n2bit_comparer_2_lt), .lt(lt), .eq(eq),
    .gt(gt));
endmodule

module cmp_swp (
  input  [3:0] in_1,
  input  [3:0] in_2,
  output [3:0] out_3,
  output [3:0] out_4
);

  wire n4bit_comparer_1_gt;

  _4bit_comparer u_4bit_comparer_1 (.X(in_1), .Y(in_2), .gt(n4bit_comparer_1_gt));  // open: lt, eq
  _4bit_swap u_4bit_swap_1 (.in_1(in_1), .in_2(in_2), .in_3(n4bit_comparer_1_gt), .out_4(out_3), .out_5(out_4));
endmodule

module _4bit_sort (
  input  [3:0] in_1,
  input  [3:0] in_2,
  input  [3:0] in_3,
  input  [3:0] in_4,
  output [3:0] out_5,
  output [3:0] out_6,
  output [3:0] out_7,
  output [3:0] out_8
);

  wire [3:0] cmp_swp_1_out_3, cmp_swp_1_out_4, cmp_swp_2_out_3, cmp_swp_2_out_4, cmp_swp_3_out_3,
       cmp_swp_3_out_4, cmp_swp_4_out_3, cmp_swp_5_out_3;

  cmp_swp cmp_swp_1 (.in_1(in_1), .in_2(in_2), .out_3(cmp_swp_1_out_3), .out_4(cmp_swp_1_out_4));
  cmp_swp cmp_swp_2 (.in_1(cmp_swp_1_out_4), .in_2(in_3), .out_3(cmp_swp_2_out_3), .out_4(cmp_swp_2_out_4));
  cmp_swp cmp_swp_3 (.in_1(cmp_swp_1_out_3), .in_2(cmp_swp_2_out_3), .out_3(cmp_swp_3_out_3), .out_4(cmp_swp_3_out_4));
  cmp_swp cmp_swp_4 (.in_1(cmp_swp_3_out_4), .in_2(cmp_swp_5_out_3), .out_3(cmp_swp_4_out_3), .out_4(out_7));
  cmp_swp cmp_swp_5 (.in_1(cmp_swp_2_out_4), .in_2(in_4), .out_3(cmp_swp_5_out_3), .out_4(out_8));
  cmp_swp cmp_swp_6 (.in_1(cmp_swp_3_out_3), .in_2(cmp_swp_4_out_3), .out_3(out_5), .out_4(out_6));
endmodule

module mod5 (
  input  In,
  output s0,
  output s1,
  output s2,
  output s3,
  output s4
);

  wire and_1_out, and_2_out, and_3_out, and_4_out, and_5_out, and_6_out, clock_1_out, not_1_out, not_2_out,
       not_3_out, not_4_out, not_5_out, not_6_out, not_7_out, not_8_out, not_10_out, not_11_out, or_1_out,
       or_2_out, register_1_q, register_2_q;

  not not_1 (not_1_out, register_1_q);
  not not_2 (not_2_out, register_2_q);
  not not_3 (not_3_out, In);
  not not_4 (not_4_out, register_1_q);
  not not_5 (not_5_out, In);
  not not_6 (not_6_out, register_2_q);
  not not_7 (not_7_out, register_1_q);
  not not_8 (not_8_out, register_2_q);
  and and_1 (and_1_out, not_1_out, register_2_q);
  and and_2 (and_2_out, register_1_q, not_2_out);
  and and_3 (and_3_out, not_3_out, not_4_out, register_2_q);
  and and_4 (and_4_out, not_5_out, register_1_q, not_6_out);
  and and_5 (and_5_out, In, not_7_out, not_8_out);
  and and_6 (and_6_out, In, register_1_q, register_2_q);
  or or_1 (or_1_out, and_1_out, and_2_out);
  or or_2 (or_2_out, and_3_out, and_4_out, and_5_out, and_6_out);
  Register #(.width(1)) register_1 (.D(or_1_out), .en(1'b1), .Q(register_1_q), .clk(clock_1_out));  // open: clr
  not not_9 (s0, 1'b1);
  Clock clock_1 (.out(clock_1_out));
  Register #(.width(1)) register_2 (.D(or_2_out), .en(1'b1), .Q(register_2_q), .clk(clock_1_out));  // open: clr
  not not_10 (not_10_out, or_1_out);
  not not_11 (not_11_out, or_2_out);
  nor nor_1 (s1, or_1_out, or_2_out);
  and and_7 (s2, not_10_out, or_2_out);
  and and_8 (s3, or_1_out, not_11_out);
  and and_9 (s4, or_1_out, or_2_out);
endmodule

module _1bit_adder (
  input  Cin,
  input  X,
  input  Y,
  output Result,
  output Cout
);

  wire and_1_out, and_2_out, xor_1_out;

  xor xor_1 (xor_1_out, X, Y);
  and and_1 (and_1_out, X, Y);
  or or_1 (Cout, and_1_out, and_2_out);
  xor xor_2 (Result, Cin, xor_1_out);
  and and_2 (and_2_out, xor_1_out, Cin);
endmodule

module _2bit_adder (
  input  in_1,
  input  [1:0] in_2,
  input  [1:0] in_3,
  output [1:0] out_4,
  output out_5
);

  wire n1bit_adder_1_cout;

  _1bit_adder u_1bit_adder_1 (.X(in_2[0]), .Y(in_3[0]), .Cin(in_1), .Cout(n1bit_adder_1_cout), .Result(out_4[0]));
  _1bit_adder u_1bit_adder_2 (.X(in_2[1]), .Y(in_3[1]), .Cin(n1bit_adder_1_cout), .Cout(out_5), .Result(out_4[1]));
endmodule

module _3bit_adder (
  input  in_1,
  input  [2:0] in_2,
  input  [2:0] in_3,
  output [2:0] out_4,
  output out_5
);

  wire n2bit_adder_1_out_5;

  _2bit_adder u_2bit_adder_1 (
    .in_2(in_2[1:0]), .in_3(in_3[1:0]), .in_1(in_1), .out_5(n2bit_adder_1_out_5), .out_4(out_4[1:0]));
  _1bit_adder u_1bit_adder_1 (.X(in_2[2]), .Y(in_3[2]), .Cin(n2bit_adder_1_out_5), .Cout(out_5), .Result(out_4[2]));
endmodule

module _4bit_adder (
  input  in_1,
  input  [3:0] in_2,
  input  [3:0] in_3,
  output [3:0] out_4,
  output out_5
);

  wire n2bit_adder_1_out_5;

  _2bit_adder u_2bit_adder_1 (
    .in_2(in_2[1:0]), .in_3(in_3[1:0]), .in_1(in_1), .out_5(n2bit_adder_1_out_5), .out_4(out_4[1:0]));
  _2bit_adder u_2bit_adder_2 (
    .in_2(in_2[3:2]), .in_3(in_3[3:2]), .in_1(n2bit_adder_1_out_5), .out_5(out_5), .out_4(out_4[3:2]));
endmodule

module _3bit_counter (
  input  Tick,
  output [2:0] Out,
  output Carry
);

  wire or_1_out;
  wire [2:0] n3bit_adder_1_out_4;

  Register #(.width(3), .trigger("falling")) register_1 (
    .D(n3bit_adder_1_out_4), .Q(Out), .clk(or_1_out));  // open: en, clr
  or or_1 (or_1_out, Tick, Carry);
  _3bit_adder u_3bit_adder_1 (.in_2(Out), .in_3(3'b001), .in_1(1'b0), .out_4(n3bit_adder_1_out_4));  // open: out_5
  and and_1 (Carry, Out[0], Out[1], Out[2]);
endmodule

module main (
  input  [2:0] in_1,
  output [3:0] out_2
);

  wire and_1_out, and_2_out, clock_1_out, counter_1_carry, n3bit_comparer_1_eq, n3bit_comparer_1_gt,
       not_1_out, not_2_out, or_1_out;
  wire [2:0] n3bit_adder_1_out_4, n3bit_counter_1_out;
  wire [3:0] _1D, _1R, _2D, _2R, _3D, _3R, multiplexer_1_out, multiplexer_2_out, n4bit_adder_1_out_4;

  Clock clock_1 (.out(clock_1_out));
  Counter #(.width(1), .max('h1), .ongoal("stay"), .trigger("falling")) counter_1 (
    .count(1'b1), .carry(counter_1_carry), .clk(clock_1_out));  // open: load, D, Q, clr
  not not_1 (not_1_out, counter_1_carry);
  and and_1 (and_1_out, clock_1_out, not_1_out);
  Register #(.width(4), .trigger("falling")) register_1 (.D(_1D), .en(1'b1), .Q(_1R), .clk(clock_1_out));  // open: clr
  and and_2 (and_2_out, counter_1_carry, not_2_out, clock_1_out);
  not not_2 (not_2_out, or_1_out);
  Multiplexer #(.width(4)) multiplexer_1 (
    .in0(_2R), .in1(4'b0001), .out(multiplexer_1_out), .sel(and_1_out), .en(1'b1));
  Multiplexer #(.width(4)) multiplexer_2 (.in0(4'b0000), .in1(_3R), .out(multiplexer_2_out), .sel(or_1_out), .en(1'b1));
  Multiplexer #(.width(4)) multiplexer_3 (.in0(multiplexer_1_out), .in1(_3R), .out(_2D), .sel(and_2_out), .en(1'b1));
  Register #(.width(4), .trigger("falling")) register_2 (.D(_2D), .en(1'b1), .Q(_2R), .clk(clock_1_out));  // open: clr
  _3bit_counter u_3bit_counter_1 (.Tick(and_2_out), .Out(n3bit_counter_1_out));  // open: Carry
  Multiplexer #(.width(4)) multiplexer_4 (.in0(_1R), .in1(_2R), .out(_1D), .sel(and_2_out), .en(1'b1));
  Multiplexer #(.select(3), .width(4)) multiplexer_5 (
    .in0(4'b0000), .in1(4'b0001), .in2(multiplexer_2_out), .in3(multiplexer_2_out), .in4(multiplexer_2_out),
    .in5(multiplexer_2_out), .in6(multiplexer_2_out), .in7(multiplexer_2_out), .out(out_2), .sel(in_1),
    .en(1'b1));
  Register #(.width(4), .trigger("high")) register_3 (.D(_3D), .en(1'b1), .Q(_3R), .clk(clock_1_out));  // open: clr
  _3bit_comparer u_3bit_comparer_1 (
    .X(n3bit_adder_1_out_4), .Y(in_1), .eq(n3bit_comparer_1_eq), .gt(n3bit_comparer_1_gt));  // open: lt
  _3bit_adder u_3bit_adder_1 (
    .in_2(n3bit_counter_1_out), .in_3(3'b001), .in_1(1'b0), .out_4(n3bit_adder_1_out_4));  // open: out_5
  or or_1 (or_1_out, n3bit_comparer_1_eq, n3bit_comparer_1_gt);
  _4bit_adder u_4bit_adder_1 (.in_2(_1R), .in_3(_2R), .in_1(1'b0), .out_4(n4bit_adder_1_out_4));  // open: out_5
  Multiplexer #(.width(4)) multiplexer_6 (.in0(_3R), .in1(n4bit_adder_1_out_4), .out(_3D), .sel(and_2_out), .en(1'b1));

  // Other names for the same wires on the sheet: Input[2:0] = in_1
endmodule

module _2x1 (
  input  [31:0] Init_Data_0_0,
  input  [31:0] Init_Data_1_0,
  input  [31:0] Data_0_0,
  input  [31:0] Data_1_0,
  input  Enabler,
  input  Clock,
  output [31:0] Output_0_0,
  output [31:0] Output_1_0
);

  register_with_init register_with_init_1 (
    .Input(Data_0_0), .Enable(Enabler), .Init_Value(Init_Data_0_0), .Clock(Clock), .Output(Output_0_0));
  register_with_init register_with_init_2 (
    .Input(Data_1_0), .Enable(Enabler), .Init_Value(Init_Data_1_0), .Clock(Clock), .Output(Output_1_0));
endmodule

module _2x2 (
  input  [31:0] Init_Data_0_0,
  input  [31:0] Init_Data_0_1,
  input  [31:0] Init_Data_1_0,
  input  [31:0] Init_Data_1_1,
  input  [31:0] Data_0_0,
  input  [31:0] Data_0_1,
  input  [31:0] Data_1_0,
  input  [31:0] Data_1_1,
  input  Enabler,
  input  Clock,
  output [31:0] Output_0_0,
  output [31:0] Output_0_1,
  output [31:0] Output_1_0,
  output [31:0] Output_1_1
);

  register_with_init register_with_init_1 (
    .Input(Data_0_0), .Enable(Enabler), .Init_Value(Init_Data_0_0), .Clock(Clock), .Output(Output_0_0));
  register_with_init register_with_init_2 (
    .Input(Data_1_0), .Enable(Enabler), .Init_Value(Init_Data_1_0), .Clock(Clock), .Output(Output_1_0));
  register_with_init register_with_init_3 (
    .Input(Data_0_1), .Enable(Enabler), .Init_Value(Init_Data_0_1), .Clock(Clock), .Output(Output_0_1));
  register_with_init register_with_init_4 (
    .Input(Data_1_1), .Enable(Enabler), .Init_Value(Init_Data_1_1), .Clock(Clock), .Output(Output_1_1));
endmodule

module _2x2__2x1 (
  input  [31:0] L_0_0,
  input  [31:0] L_0_1,
  input  [31:0] L_1_0,
  input  [31:0] L_1_1,
  input  [31:0] R_0_0,
  input  [31:0] R_1_0,
  output [31:0] Result_0_0,
  output [31:0] Result_1_0
);

  wire [31:0] multiplier_1_out, multiplier_2_out, multiplier_3_out, multiplier_4_out;

  Multiplier #(.width(32)) multiplier_1 (.a(L_0_0), .b(R_0_0), .out(multiplier_1_out));  // open: cin, cout
  Multiplier #(.width(32)) multiplier_2 (.a(L_0_1), .b(R_1_0), .out(multiplier_2_out));  // open: cin, cout
  Multiplier #(.width(32)) multiplier_3 (.a(L_1_0), .b(R_0_0), .out(multiplier_3_out));  // open: cin, cout
  Multiplier #(.width(32)) multiplier_4 (.a(L_1_1), .b(R_1_0), .out(multiplier_4_out));  // open: cin, cout
  Adder #(.width(32)) adder_1 (.a(multiplier_1_out), .b(multiplier_2_out), .out(Result_0_0));  // open: cin, cout
  Adder #(.width(32)) adder_2 (.a(multiplier_3_out), .b(multiplier_4_out), .out(Result_1_0));  // open: cin, cout
endmodule

module _2x2__2x2 (
  input  [31:0] L_0_0,
  input  [31:0] L_0_1,
  input  [31:0] L_1_0,
  input  [31:0] L_1_1,
  input  [31:0] R_0_0,
  input  [31:0] R_0_1,
  input  [31:0] R_1_0,
  input  [31:0] R_1_1,
  output [31:0] Result_0_0,
  output [31:0] Result_0_1,
  output [31:0] Result_1_0,
  output [31:0] Result_1_1
);

  wire [31:0] multiplier_1_out, multiplier_2_out, multiplier_3_out, multiplier_4_out, multiplier_5_out,
       multiplier_6_out, multiplier_7_out, multiplier_8_out;

  Multiplier #(.width(32)) multiplier_1 (.a(L_0_0), .b(R_0_0), .out(multiplier_1_out));  // open: cin, cout
  Multiplier #(.width(32)) multiplier_2 (.a(L_0_1), .b(R_1_0), .out(multiplier_2_out));  // open: cin, cout
  Multiplier #(.width(32)) multiplier_3 (.a(L_0_0), .b(R_0_1), .out(multiplier_3_out));  // open: cin, cout
  Multiplier #(.width(32)) multiplier_4 (.a(L_0_1), .b(R_1_1), .out(multiplier_4_out));  // open: cin, cout
  Multiplier #(.width(32)) multiplier_5 (.a(L_1_0), .b(R_0_0), .out(multiplier_5_out));  // open: cin, cout
  Multiplier #(.width(32)) multiplier_6 (.a(L_1_1), .b(R_1_0), .out(multiplier_6_out));  // open: cin, cout
  Multiplier #(.width(32)) multiplier_7 (.a(L_1_0), .b(R_0_1), .out(multiplier_7_out));  // open: cin, cout
  Multiplier #(.width(32)) multiplier_8 (.a(L_1_1), .b(R_1_1), .out(multiplier_8_out));  // open: cin, cout
  Adder #(.width(32)) adder_1 (.a(multiplier_1_out), .b(multiplier_2_out), .out(Result_0_0));  // open: cin, cout
  Adder #(.width(32)) adder_2 (.a(multiplier_3_out), .b(multiplier_4_out), .out(Result_0_1));  // open: cin, cout
  Adder #(.width(32)) adder_3 (.a(multiplier_5_out), .b(multiplier_6_out), .out(Result_1_0));  // open: cin, cout
  Adder #(.width(32)) adder_4 (.a(multiplier_7_out), .b(multiplier_8_out), .out(Result_1_1));  // open: cin, cout
endmodule

module shift_counter (
  input  [31:0] Input,
  input  Clock,
  output LSB,
  output gt_0
);

  wire and_1_out, counter_1_carry, not_1_out, shift_register_1_q0, shift_register_1_q1, shift_register_1_q2,
       shift_register_1_q3, shift_register_1_q4, shift_register_1_q5, shift_register_1_q6,
       shift_register_1_q7, shift_register_1_q8, shift_register_1_q9, shift_register_1_q10,
       shift_register_1_q11, shift_register_1_q12, shift_register_1_q13, shift_register_1_q14,
       shift_register_1_q15, shift_register_1_q16, shift_register_1_q17, shift_register_1_q18,
       shift_register_1_q19, shift_register_1_q20, shift_register_1_q21, shift_register_1_q22,
       shift_register_1_q23, shift_register_1_q24, shift_register_1_q25, shift_register_1_q26,
       shift_register_1_q27, shift_register_1_q28, shift_register_1_q29, shift_register_1_q30,
       shift_register_1_q31;

  and and_1 (and_1_out, Clock, not_1_out);
  not not_1 (not_1_out, counter_1_carry);
  Counter #(.width(1), .max('h1), .ongoal("stay"), .trigger("falling")) counter_1 (
    .carry(counter_1_carry), .clk(Clock));  // open: load, D, count, Q, clr
  Shift_Register #(.length(32), .trigger("falling")) shift_register_1 (
    .in(1'b0), .clk(Clock), .out(LSB), .load(and_1_out), .d0(Input[31]), .q0(shift_register_1_q0),
    .d1(Input[30]), .q1(shift_register_1_q1), .d2(Input[29]), .q2(shift_register_1_q2), .d3(Input[28]),
    .q3(shift_register_1_q3), .d4(Input[27]), .q4(shift_register_1_q4), .d5(Input[26]),
    .q5(shift_register_1_q5), .d6(Input[25]), .q6(shift_register_1_q6), .d7(Input[24]),
    .q7(shift_register_1_q7), .d8(Input[23]), .q8(shift_register_1_q8), .d9(Input[22]),
    .q9(shift_register_1_q9), .d10(Input[21]), .q10(shift_register_1_q10), .d11(Input[20]),
    .q11(shift_register_1_q11), .d12(Input[19]), .q12(shift_register_1_q12), .d13(Input[18]),
    .q13(shift_register_1_q13), .d14(Input[17]), .q14(shift_register_1_q14), .d15(Input[16]),
    .q15(shift_register_1_q15), .d16(Input[15]), .q16(shift_register_1_q16), .d17(Input[14]),
    .q17(shift_register_1_q17), .d18(Input[13]), .q18(shift_register_1_q18), .d19(Input[12]),
    .q19(shift_register_1_q19), .d20(Input[11]), .q20(shift_register_1_q20), .d21(Input[10]),
    .q21(shift_register_1_q21), .d22(Input[9]), .q22(shift_register_1_q22), .d23(Input[8]),
    .q23(shift_register_1_q23), .d24(Input[7]), .q24(shift_register_1_q24), .d25(Input[6]),
    .q25(shift_register_1_q25), .d26(Input[5]), .q26(shift_register_1_q26), .d27(Input[4]),
    .q27(shift_register_1_q27), .d28(Input[3]), .q28(shift_register_1_q28), .d29(Input[2]),
    .q29(shift_register_1_q29), .d30(Input[1]), .q30(shift_register_1_q30), .d31(Input[0]),
    .q31(shift_register_1_q31));  // open: shift, clr
  or or_1 (gt_0, shift_register_1_q0, shift_register_1_q1, shift_register_1_q2, shift_register_1_q3, shift_register_1_q4, shift_register_1_q5, shift_register_1_q6, shift_register_1_q7, shift_register_1_q8, shift_register_1_q9, shift_register_1_q10, shift_register_1_q11, shift_register_1_q12, shift_register_1_q13, shift_register_1_q14, shift_register_1_q15, shift_register_1_q17, shift_register_1_q18, shift_register_1_q19, shift_register_1_q20, shift_register_1_q21, shift_register_1_q22, shift_register_1_q23, shift_register_1_q24, shift_register_1_q25, shift_register_1_q26, shift_register_1_q27, shift_register_1_q28, shift_register_1_q29, shift_register_1_q30, shift_register_1_q31, shift_register_1_q16);
endmodule

module sqr (
  input  Enabler,
  input  Clock,
  output [31:0] Cur_0_0,
  output [31:0] Cur_0_1,
  output [31:0] Cur_1_0,
  output [31:0] Cur_1_1
);

  wire [31:0] n2x2_2x2_1_result_0_0, n2x2_2x2_1_result_0_1, n2x2_2x2_1_result_1_0, n2x2_2x2_1_result_1_1;

  _2x2 u_2x2_1 (
    .Data_0_0(n2x2_2x2_1_result_0_0), .Data_0_1(n2x2_2x2_1_result_0_1), .Data_1_0(n2x2_2x2_1_result_1_0),
    .Data_1_1(n2x2_2x2_1_result_1_1), .Enabler(Enabler), .Output_0_0(Cur_0_0), .Output_0_1(Cur_0_1),
    .Output_1_0(Cur_1_0), .Output_1_1(Cur_1_1), .Init_Data_0_0({32{1'b0}}), .Init_Data_0_1(32'h1),
    .Init_Data_1_0(32'h1), .Init_Data_1_1(32'h1), .Clock(Clock));
  _2x2__2x2 u_2x2_2x2_1 (
    .L_0_0(Cur_0_0), .L_0_1(Cur_0_1), .L_1_0(Cur_1_0), .L_1_1(Cur_1_1), .R_0_0(Cur_0_0), .R_0_1(Cur_0_1),
    .R_1_0(Cur_1_0), .R_1_1(Cur_1_1), .Result_0_0(n2x2_2x2_1_result_0_0), .Result_0_1(n2x2_2x2_1_result_0_1),
    .Result_1_0(n2x2_2x2_1_result_1_0), .Result_1_1(n2x2_2x2_1_result_1_1));
endmodule

module register_with_init (
  input  [31:0] Init_Value,
  input  [31:0] Input,
  input  Enable,
  input  Clock,
  output [31:0] Output
);

  wire and_1_out, counter_1_q, not_1_out, or_1_out;
  wire [31:0] multiplexer_1_out;

  Counter #(.width(1), .max('h1), .ongoal("stay"), .trigger("falling")) counter_1 (
    .Q(counter_1_q), .clk(Clock));  // open: load, D, count, carry, clr
  not not_1 (not_1_out, counter_1_q);
  and and_1 (and_1_out, not_1_out, Clock);
  Multiplexer #(.width(32)) multiplexer_1 (
    .in0(Init_Value), .in1(Input), .out(multiplexer_1_out), .sel(counter_1_q), .en(1'b1));
  or or_1 (or_1_out, and_1_out, Enable);
  Register #(.width(32), .trigger("falling")) register_1 (
    .D(multiplexer_1_out), .en(or_1_out), .Q(Output), .clk(Clock));  // open: clr
endmodule

module builder (
  input  [31:0] Data_0_0,
  input  [31:0] Data_0_1,
  input  [31:0] Data_1_0,
  input  [31:0] Data_1_1,
  input  Enabler,
  input  Clock,
  output [31:0] Cur_0_0,
  output [31:0] Cur_1_0
);

  wire [31:0] n2x2_2x1_1_result_0_0, n2x2_2x1_1_result_1_0;

  _2x1 u_2x1_1 (
    .Data_0_0(n2x2_2x1_1_result_0_0), .Data_1_0(n2x2_2x1_1_result_1_0), .Enabler(Enabler),
    .Output_0_0(Cur_0_0), .Output_1_0(Cur_1_0), .Init_Data_0_0({32{1'b0}}), .Init_Data_1_0(32'h1),
    .Clock(Clock));
  _2x2__2x1 u_2x2_2x1_1 (
    .L_0_0(Data_0_0), .L_0_1(Data_0_1), .L_1_0(Data_1_0), .L_1_1(Data_1_1), .R_0_0(Cur_0_0), .R_1_0(Cur_1_0),
    .Result_0_0(n2x2_2x1_1_result_0_0), .Result_1_0(n2x2_2x1_1_result_1_0));
endmodule

module main_challenge (
  input  [31:0] Input,
  output [31:0] out_2
);

  wire and_1_out, clock_1_out, not_1_out, shift_counter_1_gt_0, shift_counter_1_lsb;
  wire [31:0] builder_1_cur_0_0, sqr_1_cur_0_0, sqr_1_cur_0_1, sqr_1_cur_1_0, sqr_1_cur_1_1;

  shift_counter shift_counter_1 (
    .Input(Input), .Clock(clock_1_out), .gt_0(shift_counter_1_gt_0), .LSB(shift_counter_1_lsb));
  Clock clock_1 (.out(clock_1_out));
  sqr sqr_1 (
    .Enabler(shift_counter_1_gt_0), .Clock(clock_1_out), .Cur_0_0(sqr_1_cur_0_0), .Cur_0_1(sqr_1_cur_0_1),
    .Cur_1_0(sqr_1_cur_1_0), .Cur_1_1(sqr_1_cur_1_1));
  and and_1 (and_1_out, shift_counter_1_gt_0, shift_counter_1_lsb);
  builder builder_1 (
    .Data_0_0(sqr_1_cur_0_0), .Data_0_1(sqr_1_cur_0_1), .Data_1_0(sqr_1_cur_1_0), .Data_1_1(sqr_1_cur_1_1),
    .Enabler(and_1_out), .Clock(clock_1_out), .Cur_0_0(builder_1_cur_0_0));  // open: Cur_1_0
  not not_1 (not_1_out, shift_counter_1_gt_0);
  Multiplexer #(.width(32)) multiplexer_1 (
    .in0({32{1'b0}}), .in1(builder_1_cur_0_0), .out(out_2), .sel(not_1_out), .en(1'b1));
endmodule
